// Logisim project 16.circ as structural Verilog: 1 circuit, main circuit ADDR_16
module ADDR_16 (
  input  [15:0] A,
  input  [15:0] B,
  input  C0,
  output [15:0] S,
  output C15
);

  wire addr_4_1_c3, addr_4_2_c3, addr_4_3_c3;

  addr_4 addr_4_1 (.A(A[3:0]), .B(B[3:0]), .C0(C0), .S(S[3:0]), .C3(addr_4_1_c3));
  addr_4 addr_4_2 (.A(A[11:8]), .B(B[11:8]), .C0(addr_4_3_c3), .S(S[11:8]), .C3(addr_4_2_c3));
  addr_4 addr_4_3 (.A(A[7:4]), .B(B[7:4]), .C0(addr_4_1_c3), .S(S[7:4]), .C3(addr_4_3_c3));
  addr_4 addr_4_4 (.A(A[15:12]), .B(B[15:12]), .C0(addr_4_2_c3), .S(S[15:12]), .C3(C15));

  // Other names for the same wires on the sheet: A0_3[3:0] = A[3:0]; A4_7[3:0] = A[7:4]; A8_11[3:0] = A[11:8];
  //   A12_15[3:0] = A[15:12]; B0_3[3:0] = B[3:0]; B4_7[3:0] = B[7:4]; B8_11[3:0] = B[11:8]; B12_15[3:0] = B[15:12]
endmodule
