// Logisim project 1_fulladdr.circ as structural Verilog: 1 circuit, main circuit fulladdr
module fulladdr (
  input  A,
  input  B,
  input  C0,
  output C1,
  output S
);

  wire halfaddr_1_c, halfaddr_1_s, halfaddr_2_c;

  halfaddr halfaddr_1 (.A(A), .B(B), .C(halfaddr_1_c), .S(halfaddr_1_s));
  halfaddr halfaddr_2 (.A(halfaddr_1_s), .B(C0), .C(halfaddr_2_c), .S(S));
  or or_1 (C1, halfaddr_2_c, halfaddr_1_c);
endmodule
