// Logisim project 24decode.circ as structural Verilog: 1 circuit, main circuit main
module main (
  input  [1:0] in_1,
  output [3:0] out_2
);

  wire not_1_out, not_2_out;

  not not_1 (not_1_out, in_1[1]);
  not not_2 (not_2_out, in_1[0]);
  and and_1 (out_2[3], in_1[1], in_1[0]);
  and and_2 (out_2[2], in_1[1], not_2_out);
  and and_3 (out_2[1], not_1_out, in_1[0]);
  and and_4 (out_2[0], not_1_out, not_2_out);
endmodule
