// Logisim project 32.circ as structural Verilog: 1 circuit, main circuit add_32
module add_32 (
  input  [31:0] A,
  input  [31:0] B,
  input  C0,
  output [31:0] S,
  output C31
);

  wire addr_16_1_c15;

  ADDR_16 addr_16_1 (.A(A[15:0]), .B(B[15:0]), .C0(C0), .S(S[15:0]), .C15(addr_16_1_c15));
  ADDR_16 addr_16_2 (.A(A[31:16]), .B(B[31:16]), .C0(addr_16_1_c15), .S(S[31:16]), .C15(C31));
endmodule
