// Logisim project 32_ALU.circ as structural Verilog: 1 circuit, main circuit ALU_32
module ALU_32 (
  input  [31:0] A,
  input  [31:0] B,
  input  [2:0] OP,
  output [31:0] F,
  output SF,
  output ZF,
  output OF_1,
  output CF,
  output PF
);

  wire ABADD_C, ABSUB_C, comparator_1_lt, xor_2_out, xor_3_out;
  wire [31:0] ABADD, ABAND, ABOR, ABSLL, ABSLT, ABSUB, ABXOR, not_1_out;

  Adder #(.width(32)) adder_1 (.a(A), .b(B), .out(ABADD), .cin(1'b0), .cout(ABADD_C));
  Subtractor #(.width(32)) subtractor_1 (.a(A), .b(B), .out(ABSUB), .bin(1'b0), .bout(ABSUB_C));
  Shifter #(.width(32)) shifter_1 (.in(B), .\dist (A[4:0]), .out(ABSLT));
  Comparator #(.width(32)) comparator_1 (.a(A), .b(B), .lt(comparator_1_lt));  // open: gt, eq
  assign ABXOR = A ^ B;  // XOR_Gate xor_1, 32 bits wide
  assign ABOR = A | B;  // OR_Gate or_1, 32 bits wide
  assign ABAND = A & B;  // AND_Gate and_1, 32 bits wide
  assign ABSLL = {{31{1'b0}}, comparator_1_lt};  // Bit_Extender bit_extender_1
  assign not_1_out = ~ABOR;  // NOT_Gate not_1, 32 bits wide
  xor xor_2 (xor_2_out, B[31], A[31]);
  Multiplexer #(.select(3), .width(32)) multiplexer_1 (
    .in0(ABAND), .in1(ABOR), .in2(ABXOR), .in3(not_1_out), .in4(ABADD), .in5(ABSUB), .in6(ABSLT),
    .in7(ABSLL), .out(F), .sel(OP));
  Multiplexer #(.select(3)) multiplexer_2 (
    .in0(1'b0), .in1(1'b0), .in2(1'b0), .in3(1'b0), .in4(ABADD_C), .in5(ABSUB_C), .in6(1'b0), .in7(1'b0),
    .out(CF), .sel(OP));
  xor xor_3 (xor_3_out, xor_2_out, F[31]);
  xor xor_4 (OF_1, CF, xor_3_out);
  Comparator #(.width(32)) comparator_2 (.a(F), .b({32{1'b0}}), .eq(ZF));  // open: gt, lt
  xor odd_parity_1 (PF, F[0], F[1], F[2], F[3], F[4], F[5], F[6], F[7], F[8], F[9], F[10], F[11], F[12], F[13], F[14], F[15], F[16], F[17], F[18], F[19], F[20], F[21], F[22], F[23], F[24], F[25], F[26], F[27], F[28], F[29], F[30], F[31]);

  assign SF = F[31];

  // Other names for the same wires on the sheet: A_5[4:0] = A[4:0]; A_31 = A[31]; B_5[4:0] = B[4:0]; B_31 = B[31];
  //   Result[31:0] = F; Result2 = CF
endmodule
