// Logisim project 38decode.circ as structural Verilog: 1 circuit, main circuit main
module main (
  input  [2:0] in_1,
  input  S1,
  input  S2_f,
  input  S3_f,
  output [7:0] out_5
);

  wire nand_4_out, nand_10_out, nand_11_out, nand_12_out, nand_13_out, nand_14_out, nand_15_out;

  nand nand_1 (out_5[0], nand_11_out, nand_13_out, nand_15_out, nand_4_out);
  nand nand_2 (out_5[1], nand_10_out, nand_13_out, nand_15_out, nand_4_out);
  nand nand_3 (out_5[2], nand_11_out, nand_12_out, nand_15_out, nand_4_out);
  nand nand_4 (nand_4_out, S1, ~S2_f, ~S3_f);  // NAND_Gate
  nand nand_5 (out_5[3], nand_10_out, nand_12_out, nand_15_out, nand_4_out);
  nand nand_6 (out_5[4], nand_11_out, nand_13_out, nand_14_out, nand_4_out);
  nand nand_7 (out_5[5], nand_14_out, nand_13_out, nand_10_out, nand_4_out);
  nand nand_8 (out_5[7], nand_4_out, nand_12_out, nand_10_out, nand_14_out);
  nand nand_9 (out_5[6], nand_11_out, nand_14_out, nand_12_out, nand_4_out);
  not nand_10 (nand_10_out, nand_11_out);  // NAND_Gate
  not nand_11 (nand_11_out, in_1[2]);  // NAND_Gate
  not nand_12 (nand_12_out, nand_13_out);  // NAND_Gate
  not nand_13 (nand_13_out, in_1[1]);  // NAND_Gate
  not nand_14 (nand_14_out, nand_15_out);  // NAND_Gate
  not nand_15 (nand_15_out, in_1[0]);  // NAND_Gate
endmodule
