// Logisim project 4.circ as structural Verilog: 1 circuit, main circuit addr_4
module addr_4 (
  input  [3:0] A,
  input  [3:0] B,
  input  C0,
  output [3:0] S,
  output C3
);

  wire fulladdr_1_c1, fulladdr_2_c1, fulladdr_3_c1;

  fulladdr fulladdr_1 (.A(A[0]), .B(B[0]), .C0(C0), .C1(fulladdr_1_c1), .S(S[0]));
  fulladdr fulladdr_2 (.A(A[2]), .B(B[2]), .C0(fulladdr_3_c1), .C1(fulladdr_2_c1), .S(S[2]));
  fulladdr fulladdr_3 (.A(A[1]), .B(B[1]), .C0(fulladdr_1_c1), .C1(fulladdr_3_c1), .S(S[1]));
  fulladdr fulladdr_4 (.A(A[3]), .B(B[3]), .C0(fulladdr_2_c1), .C1(C3), .S(S[3]));
endmodule
