// Logisim project 40.circ as structural Verilog: 1 circuit, main circuit main
module main (
  input  RESET,
  input  EN,
  input  LOAD_COUNT,
  input  [7:0] in_4,
  output [7:0] out_5,
  output [7:0] out_6,
  output [7:0] out_7,
  output [7:0] out_8,
  output [7:0] out_9
);

  wire clock_1_out, counter_1_carry, counter_2_carry, counter_3_carry, counter_4_carry, not_1_out;

  Clock clock_1 (.out(clock_1_out));
  Counter counter_1 (
    .clr(RESET), .load(not_1_out), .up(1'b1), .count(EN), .clk(clock_1_out), .D(in_4),
    .carry(counter_1_carry), .Q(out_5));
  not not_1 (not_1_out, LOAD_COUNT);
  Counter counter_2 (
    .clr(RESET), .load(not_1_out), .up(1'b1), .count(counter_1_carry), .clk(clock_1_out), .D(in_4),
    .carry(counter_2_carry), .Q(out_6));
  Counter counter_3 (
    .clr(RESET), .load(not_1_out), .up(1'b1), .count(counter_2_carry), .clk(clock_1_out), .D(in_4),
    .carry(counter_3_carry), .Q(out_7));
  Counter counter_4 (
    .clr(RESET), .load(not_1_out), .up(1'b1), .count(counter_3_carry), .clk(clock_1_out), .D(in_4),
    .carry(counter_4_carry), .Q(out_8));
  Counter counter_5 (
    .clr(RESET), .load(not_1_out), .up(1'b1), .count(counter_4_carry), .clk(clock_1_out), .D(in_4), .Q(out_9));  // open: carry

  // Other names for the same wires on the sheet: data[7:0] = in_4
endmodule
