// Logisim project 8_3code.circ as structural Verilog: 1 circuit, main circuit main
module main (
  input  [7:0] in_1,
  output [2:0] out_2
);

  wire or_1_out, or_2_out, or_3_out, or_4_out, or_5_out, or_6_out;

  or or_1 (or_1_out, in_1[1], in_1[3]);
  or or_2 (or_2_out, in_1[2], in_1[3]);
  or or_3 (or_3_out, in_1[4], in_1[5]);
  or or_4 (or_4_out, or_1_out, in_1[5]);
  or or_5 (or_5_out, or_2_out, in_1[6]);
  or or_6 (or_6_out, or_3_out, in_1[6]);
  or or_7 (out_2[0], or_4_out, in_1[7]);
  or or_8 (out_2[1], or_5_out, in_1[7]);
  or or_9 (out_2[2], or_6_out, in_1[7]);
endmodule
