// Logisim project ALU32_1.circ as structural Verilog: 1 circuit, main circuit main
module main (
  input  [2:0] OP,
  input  [31:0] A,
  input  [31:0] B
);

  wire comparator_1_lt, xor_2_out;
  wire [4:0] A_5;
  wire [31:0] adder_1_out, and_1_out, bit_extender_1_out, multiplexer_1_out, not_1_out, or_1_out,
       shifter_1_out, subtractor_1_out, xor_1_out;

  Priority_Encoder #(.select(5)) priority_encoder_1 (
    .in0(A[0]), .in1(A[1]), .in2(A[2]), .in3(A[3]), .in4(A[4]), .in5(A[5]), .in6(A[6]), .in7(A[7]),
    .in8(A[8]), .in9(A[9]), .in10(A[10]), .in11(A[11]), .in12(A[12]), .in13(A[13]), .in14(A[14]),
    .in15(A[15]), .in16(A[16]), .in17(A[17]), .in18(A[18]), .in19(A[19]), .in20(A[20]), .in21(A[21]),
    .in22(A[22]), .in23(A[23]), .in24(A[24]), .in25(A[25]), .in26(A[26]), .in27(A[27]), .in28(A[28]),
    .in29(A[29]), .in30(A[30]), .in31(A[31]), .out(A_5), .en_in(1'b1));  // open: gs, en_out
  assign or_1_out = A | B;  // OR_Gate or_1, 32 bits wide
  assign not_1_out = ~or_1_out;  // NOT_Gate not_1, 32 bits wide
  Adder #(.width(32)) adder_1 (.a(A), .b(B), .out(adder_1_out));  // open: cin, cout
  Subtractor #(.width(32)) subtractor_1 (.a(A), .b(B), .out(subtractor_1_out));  // open: bin, bout
  Comparator #(.width(32)) comparator_1 (.a(A), .b(B), .lt(comparator_1_lt));  // open: gt, eq
  Shifter #(.width(32)) shifter_1 (.in(B), .\dist (A_5), .out(shifter_1_out));
  assign xor_1_out = A ^ B;  // XOR_Gate xor_1, 32 bits wide
  assign and_1_out = A & B;  // AND_Gate and_1, 32 bits wide
  assign bit_extender_1_out = {{31{1'b0}}, comparator_1_lt};  // Bit_Extender bit_extender_1
  Multiplexer #(.select(3), .width(32)) multiplexer_1 (
    .in0(and_1_out), .in1(or_1_out), .in2(xor_1_out), .in3(not_1_out), .in4(adder_1_out),
    .in5(subtractor_1_out), .in6(bit_extender_1_out), .in7(shifter_1_out), .out(multiplexer_1_out), .sel(OP));
  xor xor_2 (xor_2_out, A[31], B[31]);
  // XOR_Gate xor_3 has open pins: in0=xor_2_out, out=open
endmodule
