// Logisim project ALUCONTROL__lite.circ as structural Verilog: 1 circuit, main circuit ALUcontrol_lite
module ALUcontrol_lite (
  input  [5:0] funcode,
  input  [4:0] ALUop,
  output V,
  output JRN,
  output [3:0] ALUctrl,
  output judge,
  output lo,
  output hi
);

  wire a_nd, add, addi, addiu, addu, ALU_0000, ALU_0001, ALU_0010, ALU_0011, ALU_0100, ALU_0101, ALU_0110,
       ALU_0111, ALU_1000, ALU_1001, ALU_1010, ALU_1011, ALU_1100, ALU_1101, ALU_1110, andi, beq, bne, lb,
       lbu, lh, lhu, lw, not_1_out, not_2_out, not_3_out, not_4_out, not_5_out, not_6_out, not_7_out,
       not_8_out, not_9_out, not_10_out, not_11_out, not_12_out, not_13_out, not_14_out, not_15_out,
       not_16_out, not_17_out, not_18_out, not_19_out, not_20_out, not_21_out, not_22_out, not_23_out,
       not_24_out, not_25_out, not_26_out, not_27_out, not_28_out, not_29_out, not_30_out, not_31_out,
       not_32_out, not_33_out, not_34_out, not_35_out, not_36_out, not_37_out, not_38_out, not_39_out,
       not_40_out, not_41_out, not_42_out, not_43_out, not_44_out, not_45_out, not_46_out, not_47_out,
       not_48_out, not_49_out, not_50_out, not_51_out, not_52_out, not_53_out, not_54_out, not_55_out,
       not_56_out, not_57_out, not_58_out, not_59_out, not_60_out, not_61_out, not_62_out, not_63_out,
       not_64_out, not_65_out, not_66_out, not_67_out, not_68_out, not_69_out, not_70_out, not_71_out,
       not_72_out, not_73_out, not_74_out, not_75_out, not_76_out, not_77_out, not_78_out, not_79_out,
       not_80_out, not_81_out, not_82_out, not_83_out, not_84_out, not_85_out, not_86_out, not_87_out,
       not_88_out, not_89_out, not_90_out, not_91_out, not_92_out, not_93_out, not_94_out, not_95_out,
       not_96_out, not_97_out, not_98_out, not_99_out, not_100_out, not_101_out, not_102_out, not_103_out,
       not_104_out, not_105_out, not_106_out, not_107_out, not_108_out, not_109_out, not_110_out,
       not_111_out, not_112_out, not_113_out, not_114_out, not_115_out, not_116_out, not_117_out,
       not_118_out, not_119_out, not_120_out, not_121_out, not_122_out, not_123_out, not_124_out,
       not_125_out, not_126_out, not_127_out, not_128_out, not_129_out, not_130_out, not_131_out,
       not_132_out, not_133_out, not_134_out, not_135_out, not_136_out, not_137_out, not_138_out,
       not_139_out, not_140_out, not_141_out, not_142_out, not_143_out, not_144_out, not_145_out,
       not_146_out, not_147_out, not_148_out, not_149_out, not_150_out, not_151_out, not_152_out,
       not_153_out, not_154_out, not_155_out, not_156_out, not_157_out, not_158_out, not_159_out,
       not_160_out, not_161_out, not_162_out, not_163_out, not_164_out, not_165_out, not_166_out,
       not_167_out, not_168_out, not_169_out, not_170_out, not_171_out, not_172_out, not_173_out,
       not_174_out, not_175_out, not_176_out, not_177_out, not_178_out, not_179_out, not_180_out,
       not_181_out, not_182_out, not_183_out, not_184_out, not_185_out, not_186_out, not_187_out,
       not_188_out, not_189_out, not_190_out, not_191_out, not_192_out, not_193_out, not_194_out,
       not_195_out, not_196_out, not_197_out, not_198_out, not_199_out, not_200_out, not_201_out,
       not_202_out, not_203_out, not_204_out, not_205_out, not_206_out, not_207_out, not_208_out,
       not_209_out, not_210_out, not_211_out, not_212_out, not_213_out, not_214_out, not_215_out,
       not_216_out, not_217_out, o_r, ori, sb, sh, sl_l, sl_lv, sr_a, sr_av, sr_l, sr_lv, sub, subu, sw,
       xo_r, xori;

  not not_1 (not_1_out, ALUop[4]);
  not not_2 (not_2_out, ALUop[3]);
  not not_3 (not_3_out, ALUop[4]);
  not not_4 (not_4_out, ALUop[3]);
  not not_5 (not_5_out, ALUop[4]);
  not not_6 (not_6_out, ALUop[3]);
  not not_7 (not_7_out, ALUop[4]);
  not not_8 (not_8_out, ALUop[3]);
  not not_9 (not_9_out, ALUop[4]);
  not not_10 (not_10_out, ALUop[3]);
  not not_11 (not_11_out, funcode[1]);
  not not_12 (not_12_out, funcode[2]);
  not not_13 (not_13_out, funcode[3]);
  not not_14 (not_14_out, funcode[4]);
  not not_15 (not_15_out, ALUop[4]);
  not not_16 (not_16_out, ALUop[3]);
  not not_17 (not_17_out, ALUop[0]);
  not not_18 (not_18_out, ALUop[1]);
  not not_19 (not_19_out, ALUop[2]);
  not not_20 (not_20_out, funcode[0]);
  not not_21 (not_21_out, funcode[1]);
  not not_22 (not_22_out, funcode[2]);
  not not_23 (not_23_out, funcode[3]);
  not not_24 (not_24_out, funcode[4]);
  not not_25 (not_25_out, funcode[2]);
  not not_26 (not_26_out, funcode[5]);
  not not_27 (not_27_out, funcode[1]);
  not not_28 (not_28_out, funcode[2]);
  not not_29 (not_29_out, funcode[5]);
  not not_30 (not_30_out, funcode[0]);
  not not_31 (not_31_out, funcode[1]);
  not not_32 (not_32_out, funcode[2]);
  not not_33 (not_33_out, funcode[5]);
  not not_34 (not_34_out, funcode[1]);
  not not_35 (not_35_out, funcode[3]);
  not not_36 (not_36_out, funcode[4]);
  not not_37 (not_37_out, funcode[0]);
  not not_38 (not_38_out, funcode[1]);
  not not_39 (not_39_out, funcode[3]);
  not not_40 (not_40_out, funcode[4]);
  not not_41 (not_41_out, funcode[5]);
  not not_42 (not_42_out, funcode[3]);
  not not_43 (not_43_out, funcode[4]);
  not not_44 (not_44_out, funcode[5]);
  not not_45 (not_45_out, funcode[0]);
  not not_46 (not_46_out, funcode[3]);
  not not_47 (not_47_out, funcode[4]);
  not not_48 (not_48_out, funcode[5]);
  not not_49 (not_49_out, funcode[0]);
  not not_50 (not_50_out, funcode[3]);
  not not_51 (not_51_out, funcode[4]);
  not not_52 (not_52_out, ALUop[4]);
  not not_53 (not_53_out, ALUop[3]);
  not not_54 (not_54_out, ALUop[0]);
  not not_55 (not_55_out, ALUop[1]);
  not not_56 (not_56_out, ALUop[2]);
  not not_57 (not_57_out, ALUop[0]);
  not not_58 (not_58_out, ALUop[1]);
  not not_59 (not_59_out, ALUop[2]);
  not not_60 (not_60_out, ALUop[0]);
  not not_61 (not_61_out, ALUop[1]);
  not not_62 (not_62_out, ALUop[2]);
  not not_63 (not_63_out, ALUop[4]);
  not not_64 (not_64_out, ALUop[3]);
  not not_65 (not_65_out, ALUop[0]);
  not not_66 (not_66_out, ALUop[1]);
  not not_67 (not_67_out, ALUop[2]);
  not not_68 (not_68_out, ALUop[4]);
  not not_69 (not_69_out, ALUop[3]);
  not not_70 (not_70_out, ALUop[0]);
  not not_71 (not_71_out, ALUop[1]);
  not not_72 (not_72_out, ALUop[2]);
  not not_73 (not_73_out, ALUop[4]);
  not not_74 (not_74_out, ALUop[3]);
  not not_75 (not_75_out, ALUop[0]);
  not not_76 (not_76_out, ALUop[1]);
  not not_77 (not_77_out, ALUop[2]);
  not not_78 (not_78_out, ALUop[0]);
  not not_79 (not_79_out, ALUop[1]);
  not not_80 (not_80_out, ALUop[2]);
  not not_81 (not_81_out, ALUop[0]);
  not not_82 (not_82_out, ALUop[1]);
  not not_83 (not_83_out, ALUop[2]);
  not not_84 (not_84_out, ALUop[0]);
  not not_85 (not_85_out, ALUop[1]);
  not not_86 (not_86_out, ALUop[2]);
  and and_1 (addu, not_52_out, not_53_out, not_54_out, not_55_out, not_56_out, funcode[0], not_11_out, not_12_out, not_13_out, not_14_out, funcode[5]);
  and and_2 (add, not_15_out, not_16_out, not_17_out, not_18_out, not_19_out, not_20_out, not_21_out, not_22_out, not_23_out, not_24_out, funcode[5]);
  and and_3 (ALU_1110, not_1_out, not_2_out, not_57_out, not_58_out, not_59_out, funcode[0], funcode[1], not_25_out, funcode[3], funcode[4], not_26_out);
  and and_4 (ALU_1101, not_3_out, not_4_out, not_60_out, not_61_out, not_62_out, funcode[0], not_27_out, not_28_out, funcode[3], funcode[4], not_29_out);
  and and_5 (ALU_0011, not_63_out, not_64_out, not_65_out, not_66_out, not_67_out, not_30_out, not_31_out, not_32_out, funcode[3], funcode[4], not_33_out);
  and and_6 (o_r, not_68_out, not_69_out, not_70_out, not_71_out, not_72_out, funcode[0], not_34_out, funcode[2], not_35_out, not_36_out, funcode[5]);
  and and_7 (sl_lv, not_73_out, not_74_out, not_75_out, not_76_out, not_77_out, not_37_out, not_38_out, funcode[2], not_39_out, not_40_out, not_41_out);
  and and_8 (sr_av, not_5_out, not_6_out, not_78_out, not_79_out, not_80_out, funcode[0], funcode[1], funcode[2], not_42_out, not_43_out, not_44_out);
  and and_9 (sr_lv, not_7_out, not_8_out, not_81_out, not_82_out, not_83_out, not_45_out, funcode[1], funcode[2], not_46_out, not_47_out, not_48_out);
  and and_10 (xo_r, not_9_out, not_10_out, not_84_out, not_85_out, not_86_out, not_49_out, funcode[1], funcode[2], not_50_out, not_51_out, funcode[5]);
  not not_87 (not_87_out, ALUop[4]);
  not not_88 (not_88_out, ALUop[3]);
  not not_89 (not_89_out, ALUop[4]);
  not not_90 (not_90_out, ALUop[3]);
  not not_91 (not_91_out, ALUop[4]);
  not not_92 (not_92_out, ALUop[3]);
  not not_93 (not_93_out, ALUop[4]);
  not not_94 (not_94_out, ALUop[3]);
  not not_95 (not_95_out, funcode[0]);
  not not_96 (not_96_out, funcode[1]);
  not not_97 (not_97_out, funcode[3]);
  not not_98 (not_98_out, funcode[4]);
  not not_99 (not_99_out, ALUop[4]);
  not not_100 (not_100_out, ALUop[3]);
  not not_101 (not_101_out, ALUop[0]);
  not not_102 (not_102_out, ALUop[1]);
  not not_103 (not_103_out, ALUop[2]);
  not not_104 (not_104_out, funcode[2]);
  not not_105 (not_105_out, funcode[3]);
  not not_106 (not_106_out, funcode[4]);
  not not_107 (not_107_out, ALUop[4]);
  not not_108 (not_108_out, ALUop[3]);
  not not_109 (not_109_out, ALUop[0]);
  not not_110 (not_110_out, ALUop[1]);
  not not_111 (not_111_out, ALUop[2]);
  not not_112 (not_112_out, ALUop[0]);
  not not_113 (not_113_out, ALUop[1]);
  not not_114 (not_114_out, ALUop[2]);
  not not_115 (not_115_out, funcode[0]);
  not not_116 (not_116_out, funcode[1]);
  not not_117 (not_117_out, funcode[2]);
  not not_118 (not_118_out, funcode[4]);
  not not_119 (not_119_out, funcode[5]);
  not not_120 (not_120_out, ALUop[0]);
  not not_121 (not_121_out, ALUop[1]);
  not not_122 (not_122_out, ALUop[2]);
  not not_123 (not_123_out, funcode[0]);
  not not_124 (not_124_out, funcode[2]);
  not not_125 (not_125_out, funcode[5]);
  not not_126 (not_126_out, ALUop[4]);
  not not_127 (not_127_out, ALUop[3]);
  not not_128 (not_128_out, ALUop[0]);
  not not_129 (not_129_out, ALUop[1]);
  not not_130 (not_130_out, ALUop[2]);
  not not_131 (not_131_out, funcode[3]);
  not not_132 (not_132_out, funcode[4]);
  not not_133 (not_133_out, ALUop[4]);
  not not_134 (not_134_out, ALUop[3]);
  not not_135 (not_135_out, ALUop[0]);
  not not_136 (not_136_out, ALUop[1]);
  not not_137 (not_137_out, ALUop[2]);
  not not_138 (not_138_out, funcode[0]);
  not not_139 (not_139_out, funcode[1]);
  not not_140 (not_140_out, funcode[2]);
  not not_141 (not_141_out, funcode[3]);
  not not_142 (not_142_out, funcode[4]);
  not not_143 (not_143_out, funcode[5]);
  not not_144 (not_144_out, ALUop[4]);
  not not_145 (not_145_out, ALUop[3]);
  not not_146 (not_146_out, ALUop[0]);
  not not_147 (not_147_out, ALUop[1]);
  not not_148 (not_148_out, ALUop[2]);
  not not_149 (not_149_out, funcode[2]);
  not not_150 (not_150_out, funcode[3]);
  not not_151 (not_151_out, funcode[4]);
  not not_152 (not_152_out, funcode[5]);
  not not_153 (not_153_out, ALUop[0]);
  not not_154 (not_154_out, ALUop[1]);
  not not_155 (not_155_out, ALUop[2]);
  not not_156 (not_156_out, funcode[0]);
  not not_157 (not_157_out, funcode[2]);
  not not_158 (not_158_out, funcode[3]);
  not not_159 (not_159_out, funcode[4]);
  not not_160 (not_160_out, funcode[5]);
  not not_161 (not_161_out, ALUop[0]);
  not not_162 (not_162_out, ALUop[1]);
  not not_163 (not_163_out, ALUop[2]);
  not not_164 (not_164_out, funcode[0]);
  not not_165 (not_165_out, funcode[2]);
  not not_166 (not_166_out, funcode[3]);
  not not_167 (not_167_out, funcode[4]);
  and and_11 (subu, not_99_out, not_100_out, not_101_out, not_102_out, not_103_out, funcode[0], funcode[1], not_104_out, not_105_out, not_106_out, funcode[5]);
  and and_12 (a_nd, not_107_out, not_108_out, not_109_out, not_110_out, not_111_out, not_95_out, not_96_out, funcode[2], not_97_out, not_98_out, funcode[5]);
  and and_13 (JRN, not_87_out, not_88_out, not_112_out, not_113_out, not_114_out, not_115_out, not_116_out, not_117_out, funcode[3], not_118_out, not_119_out);
  and and_14 (ALU_0100, not_89_out, not_90_out, not_120_out, not_121_out, not_122_out, not_123_out, funcode[1], not_124_out, funcode[3], funcode[4], not_125_out);
  and and_15 (ALU_1010, not_126_out, not_127_out, not_128_out, not_129_out, not_130_out, funcode[0], funcode[1], funcode[2], not_131_out, not_132_out, funcode[5]);
  and and_16 (sl_l, not_133_out, not_134_out, not_135_out, not_136_out, not_137_out, not_138_out, not_139_out, not_140_out, not_141_out, not_142_out, not_143_out);
  and and_17 (sr_a, not_144_out, not_145_out, not_146_out, not_147_out, not_148_out, funcode[0], funcode[1], not_149_out, not_150_out, not_151_out, not_152_out);
  and and_18 (sr_l, not_91_out, not_92_out, not_153_out, not_154_out, not_155_out, not_156_out, funcode[1], not_157_out, not_158_out, not_159_out, not_160_out);
  and and_19 (sub, not_93_out, not_94_out, not_161_out, not_162_out, not_163_out, not_164_out, funcode[1], not_165_out, not_166_out, not_167_out, funcode[5]);
  not not_168 (not_168_out, ALUop[1]);
  not not_169 (not_169_out, ALUop[2]);
  not not_170 (not_170_out, ALUop[3]);
  not not_171 (not_171_out, ALUop[4]);
  not not_172 (not_172_out, ALUop[0]);
  not not_173 (not_173_out, ALUop[2]);
  not not_174 (not_174_out, ALUop[3]);
  not not_175 (not_175_out, ALUop[4]);
  not not_176 (not_176_out, ALUop[2]);
  not not_177 (not_177_out, ALUop[3]);
  not not_178 (not_178_out, ALUop[4]);
  not not_179 (not_179_out, ALUop[0]);
  not not_180 (not_180_out, ALUop[1]);
  not not_181 (not_181_out, ALUop[3]);
  not not_182 (not_182_out, ALUop[4]);
  not not_183 (not_183_out, ALUop[1]);
  not not_184 (not_184_out, ALUop[3]);
  not not_185 (not_185_out, ALUop[4]);
  not not_186 (not_186_out, ALUop[0]);
  not not_187 (not_187_out, ALUop[3]);
  not not_188 (not_188_out, ALUop[4]);
  not not_189 (not_189_out, ALUop[3]);
  not not_190 (not_190_out, ALUop[4]);
  not not_191 (not_191_out, ALUop[0]);
  not not_192 (not_192_out, ALUop[1]);
  not not_193 (not_193_out, ALUop[2]);
  not not_194 (not_194_out, ALUop[4]);
  not not_195 (not_195_out, ALUop[1]);
  not not_196 (not_196_out, ALUop[2]);
  not not_197 (not_197_out, ALUop[4]);
  not not_198 (not_198_out, ALUop[0]);
  not not_199 (not_199_out, ALUop[2]);
  not not_200 (not_200_out, ALUop[4]);
  not not_201 (not_201_out, ALUop[2]);
  not not_202 (not_202_out, ALUop[4]);
  not not_203 (not_203_out, ALUop[0]);
  not not_204 (not_204_out, ALUop[1]);
  not not_205 (not_205_out, ALUop[4]);
  not not_206 (not_206_out, ALUop[1]);
  not not_207 (not_207_out, ALUop[4]);
  not not_208 (not_208_out, ALUop[0]);
  not not_209 (not_209_out, ALUop[4]);
  not not_210 (not_210_out, ALUop[4]);
  not not_211 (not_211_out, ALUop[0]);
  not not_212 (not_212_out, ALUop[1]);
  not not_213 (not_213_out, ALUop[2]);
  not not_214 (not_214_out, ALUop[3]);
  not not_215 (not_215_out, ALUop[1]);
  not not_216 (not_216_out, ALUop[2]);
  not not_217 (not_217_out, ALUop[3]);
  and and_20 (addi, ALUop[0], not_168_out, not_169_out, not_170_out, not_171_out);
  and and_21 (addiu, not_172_out, ALUop[1], not_173_out, not_174_out, not_175_out);
  and and_22 (andi, ALUop[0], ALUop[1], not_176_out, not_177_out, not_178_out);
  and and_23 (beq, not_179_out, not_180_out, ALUop[2], not_181_out, not_182_out);
  and and_24 (bne, ALUop[0], not_183_out, ALUop[2], not_184_out, not_185_out);
  and and_25 (lb, not_186_out, ALUop[1], ALUop[2], not_187_out, not_188_out);
  and and_26 (lbu, ALUop[0], ALUop[1], ALUop[2], not_189_out, not_190_out);
  and and_27 (lh, not_191_out, not_192_out, not_193_out, ALUop[3], not_194_out);
  and and_28 (lhu, ALUop[0], not_195_out, not_196_out, ALUop[3], not_197_out);
  and and_29 (lw, not_198_out, ALUop[1], not_199_out, ALUop[3], not_200_out);
  and and_30 (ori, ALUop[0], ALUop[1], not_201_out, ALUop[3], not_202_out);
  and and_31 (sb, not_203_out, not_204_out, ALUop[2], ALUop[3], not_205_out);
  and and_32 (sh, ALUop[0], not_206_out, ALUop[2], ALUop[3], not_207_out);
  and and_33 (ALU_1011, not_208_out, ALUop[1], ALUop[2], ALUop[3], not_209_out);
  and and_34 (ALU_1100, ALUop[0], ALUop[1], ALUop[2], ALUop[3], not_210_out);
  and and_35 (sw, not_211_out, not_212_out, not_213_out, not_214_out, ALUop[4]);
  and and_36 (xori, ALUop[0], not_215_out, not_216_out, not_217_out, ALUop[4]);
  or or_1 (ALU_0111, a_nd, andi);
  or or_2 (ALU_0110, beq, bne, subu, sub);
  or or_3 (ALU_1000, o_r, ori);
  or or_4 (ALU_0000, sl_l, sl_lv);
  or or_5 (ALU_0001, sr_a, sr_av);
  or or_6 (ALU_0010, sr_l, sr_lv);
  or or_7 (ALU_1001, xo_r, xori);
  or or_8 (ALU_0101, add, addi, addiu, addu, lbu, lb, lh, lhu, lw, sb, sh, sw);
  or or_9 (ALUctrl[0], ALU_0101, ALU_0111, ALU_0011, ALU_0001, ALU_1001, ALU_1101, ALU_1011);
  or or_10 (hi, ALU_0011, ALU_1101, ALU_0100, ALU_1110);
  or or_11 (ALUctrl[1], ALU_0111, ALU_0110, ALU_1110, ALU_0011, ALU_1010, ALU_1011, ALU_0010);
  or or_12 (ALUctrl[2], ALU_0101, ALU_0111, ALU_0110, ALU_0100, ALU_1110, ALU_1101, ALU_1100);
  or or_13 (ALUctrl[3], ALU_1001, ALU_1000, ALU_1100, ALU_1011, ALU_1010, ALU_1101, ALU_1110);
  or or_14 (lo, ALU_0011, ALU_1101, ALU_0100, ALU_1110);
  or or_15 (judge, add, addi, sub);
  or or_16 (V, sl_l, sr_l, sr_a);

  // Other names for the same wires on the sheet: div = ALU_0100; divu = ALU_1110; OP0 = funcode[0]; OP1 = funcode[1];
  //   OP2 = funcode[2]; OP3 = funcode[3]; OP4 = funcode[4]; OP5 = funcode[5]; jr = JRN; mult = ALU_0011;
  //   multu = ALU_1101; no_r = ALU_1010; slti = ALU_1011; sltiu = ALU_1100

  // Notes on the sheet:
  //   输入
  //   add
  //   divu
  //   multu
  //   mult
  //   or
  //   sllv
  //   srav
  //   srlv
  //   xor
  //   addu
  //   ALU控制译码器
  //   输出
  //   and
  //   jr
  //   div
  //   srl
  //   sub
  //   subu
  //   nor
  //   sll
  //   sra
  //   andi
  //   beq
  //   lb
  //   lbu
  //   lh
  //   lhu
  //   lw
  //   ori
  //   sh
  //   sw
  //   xori
  //   addi
  //   addiu
  //   bne
  //   sb
  //   slti
  //   sltiu
endmodule
