// Logisim project ALU_lite_32.circ as structural Verilog: 1 circuit, main circuit ALU_Lite
module ALU_Lite (
  input  [31:0] A,
  input  [31:0] B,
  input  [3:0] OP,
  output [31:0] F,
  output SF,
  output ZF,
  output OF_1,
  output CF,
  output PF,
  output [31:0] F_2,
  output UOF_1
);

  wire ABADD_C, ABSUB_C, comparator_1_lt, comparator_2_lt, xor_2_out, xor_3_out;
  wire [31:0] ABADD, ABAND, ABDIV_Quotient, ABDIV_QuotientU, ABDIV_Remainder, ABDIV_RemainderU, ABMUIT0_31,
       ABMUIT0_31U, ABMUIT32_64, ABMUIT32_64U, ABOR, ABSLL, ABSLT, ABSLTU, ABSRA, ABSRL, ABSUB, ABXOR,
       not_1_out;

  Adder #(.width(32)) adder_1 (.a(A), .b(B), .out(ABADD), .cin(1'b0), .cout(ABADD_C));
  Subtractor #(.width(32)) subtractor_1 (.a(A), .b(B), .out(ABSUB), .bin(1'b0), .bout(ABSUB_C));
  Shifter #(.width(32)) shifter_1 (.in(B), .\dist (A[4:0]), .out(ABSLL));
  Shifter #(.shift("ar"), .width(32)) shifter_2 (.in(B), .\dist (A[4:0]), .out(ABSRA));
  Shifter #(.shift("lr"), .width(32)) shifter_3 (.in(B), .\dist (A[4:0]), .out(ABSRL));
  Comparator #(.width(32)) comparator_1 (.a(A), .b(B), .lt(comparator_1_lt));  // open: gt, eq
  Multiplier #(.mode("twosComplement"), .width(32)) multiplier_1 (
    .a(A), .b(B), .out(ABMUIT0_31), .cout(ABMUIT32_64));  // open: cin
  Divider #(.mode("twosComplement"), .width(32)) divider_1 (
    .a(A), .b(B), .out(ABDIV_Quotient), .rem(ABDIV_Remainder));  // open: upper
  Comparator #(.mode("unsigned"), .width(32)) comparator_2 (.a(A), .b(B), .lt(comparator_2_lt));  // open: gt, eq
  Multiplier #(.width(32)) multiplier_2 (.a(A), .b(B), .out(ABMUIT0_31U), .cout(ABMUIT32_64U));  // open: cin
  Divider #(.width(32)) divider_2 (.a(A), .b(B), .out(ABDIV_QuotientU), .rem(ABDIV_RemainderU));  // open: upper
  assign ABXOR = A ^ B;  // XOR_Gate xor_1, 32 bits wide
  assign ABOR = A | B;  // OR_Gate or_1, 32 bits wide
  assign ABAND = A & B;  // AND_Gate and_1, 32 bits wide
  assign ABSLT = {{31{1'b0}}, comparator_1_lt};  // Bit_Extender bit_extender_1
  assign ABSLTU = {{31{1'b0}}, comparator_2_lt};  // Bit_Extender bit_extender_2
  assign not_1_out = ~ABOR;  // NOT_Gate not_1, 32 bits wide
  Multiplexer #(.select(4), .width(32)) multiplexer_1 (
    .in0(ABSLL), .in1(ABSRA), .in2(ABSRL), .in3(ABMUIT0_31), .in4(ABDIV_Quotient), .in5(ABADD), .in6(ABSUB),
    .in7(ABAND), .in8(ABOR), .in9(ABXOR), .in10(not_1_out), .in11(ABSLT), .in12(ABSLTU), .in13(ABMUIT0_31U),
    .in14(ABDIV_QuotientU), .in15({32{1'b1}}), .out(F), .sel(OP));
  Multiplexer #(.select(4), .width(32)) multiplexer_2 (
    .in0({32{1'b0}}), .in1({32{1'b0}}), .in2({32{1'b0}}), .in3(ABMUIT32_64), .in4(ABDIV_Remainder),
    .in5({32{1'b0}}), .in6({32{1'b0}}), .in7({32{1'b0}}), .in8({32{1'b0}}), .in9({32{1'b0}}),
    .in10({32{1'b0}}), .in11({32{1'b0}}), .in12({32{1'b0}}), .in13(ABMUIT32_64U), .in14(ABDIV_RemainderU),
    .in15({32{1'b0}}), .out(F_2), .sel(OP));
  Multiplexer #(.select(4)) multiplexer_3 (
    .in0(1'b0), .in1(1'b0), .in2(1'b0), .in3(1'b0), .in4(1'b0), .in5(ABADD_C), .in6(ABSUB_C), .in7(1'b0),
    .in8(1'b0), .in9(1'b0), .in10(1'b0), .in11(1'b0), .in12(1'b0), .in13(1'b0), .in14(1'b0), .in15(1'b0),
    .out(CF), .sel(OP));
  Comparator #(.width(32)) comparator_3 (.a(F), .b({32{1'b0}}), .eq(ZF));  // open: gt, lt
  xor xor_2 (xor_2_out, B[31], A[31]);
  xor odd_parity_1 (PF, F[0], F[1], F[2], F[3], F[4], F[5], F[6], F[7], F[8], F[9], F[10], F[11], F[12], F[13], F[14], F[15], F[16], F[17], F[18], F[19], F[20], F[21], F[22], F[23], F[24], F[25], F[26], F[27], F[28], F[29], F[30], F[31]);
  xor xor_3 (xor_3_out, xor_2_out, F[31]);
  xor xor_4 (OF_1, CF, xor_3_out);

  assign SF = F[31];
  assign UOF_1 = CF;

  // Other names for the same wires on the sheet: A_5[4:0] = A[4:0]; A_31 = A[31]; ADD_SUB_OF = CF; B_5[4:0] = B[4:0];
  //   B_31 = B[31]; Result[31:0] = F; Result2[31:0] = F_2
endmodule
