// Logisim project ALUctrl.circ as structural Verilog: 1 circuit, main circuit ALUctrl1
module ALUctrl1 (
  input  [5:0] funcode,
  input  [2:0] ALUop,
  output [2:0] ALUctrl
);

  wire addu, beq, lui, lw, not_1_out, not_2_out, not_3_out, not_4_out, not_5_out, not_6_out, not_7_out,
       not_8_out, not_9_out, not_10_out, not_11_out, not_12_out, not_13_out, not_14_out, not_15_out,
       not_16_out, not_17_out, not_18_out, not_19_out, not_20_out, ori, subu, sw;

  not not_1 (not_1_out, ALUop[0]);
  not not_2 (not_2_out, ALUop[2]);
  not not_3 (not_3_out, ALUop[0]);
  not not_4 (not_4_out, ALUop[1]);
  not not_5 (not_5_out, ALUop[2]);
  not not_6 (not_6_out, funcode[1]);
  not not_7 (not_7_out, funcode[2]);
  not not_8 (not_8_out, funcode[3]);
  not not_9 (not_9_out, funcode[4]);
  or or_1 (ALUctrl[0], beq, subu, lui);
  or or_2 (ALUctrl[1], addu, beq, lw, lui, sw, subu);
  and and_1 (beq, not_1_out, ALUop[1], not_2_out);
  and and_2 (addu, not_3_out, not_4_out, not_5_out, funcode[0], not_6_out, not_7_out, not_8_out, not_9_out, funcode[5]);
  not not_10 (not_10_out, ALUop[2]);
  or or_3 (ALUctrl[2], lui, ori);
  and and_3 (lui, ALUop[0], ALUop[1], not_10_out);
  not not_11 (not_11_out, ALUop[1]);
  not not_12 (not_12_out, ALUop[2]);
  and and_4 (lw, ALUop[0], not_11_out, not_12_out);
  and and_5 (ori, ALUop[0], ALUop[1], ALUop[2]);
  not not_13 (not_13_out, funcode[2]);
  not not_14 (not_14_out, funcode[3]);
  not not_15 (not_15_out, funcode[4]);
  not not_16 (not_16_out, ALUop[0]);
  not not_17 (not_17_out, ALUop[1]);
  not not_18 (not_18_out, ALUop[2]);
  and and_6 (subu, not_16_out, not_17_out, not_18_out, funcode[0], funcode[1], not_13_out, not_14_out, not_15_out, funcode[5]);
  not not_19 (not_19_out, ALUop[1]);
  not not_20 (not_20_out, ALUop[2]);
  and and_7 (sw, ALUop[0], not_19_out, not_20_out);

  // Other names for the same wires on the sheet: ALUctrl2 = ALUctrl[0]; ALUctrl0 = ALUctrl[2]; OP0 = funcode[0];
  //   OP1 = funcode[1]; OP2 = funcode[2]; OP3 = funcode[3]; OP4 = funcode[4]; OP5 = funcode[5]

  // Notes on the sheet:
  //   输入
  //   beq
  //   addu
  //   lui
  //   ALU控制译码器
  //   输出
  //   lw
  //   ori
  //   subu
  //   sw
endmodule
