// Logisim project CONTROL.circ as structural Verilog: 1 circuit, main circuit CONTROL
module CONTROL (
  input  [5:0] FUNCCODE,
  input  [5:0] OPCODE,
  output RegDst,
  output MemRead,
  output MemtoReg2,
  output ALUSrc,
  output MemWrite,
  output EXTOp,
  output [2:0] ALUctrl,
  output RegWrite,
  output MemtoReg1,
  output Branch
);

  wire [2:0] mcu1_1_aluop;

  MCU1 mcu1_1 (
    .OP_CODE(OPCODE), .RegDst(RegDst), .MemRead(MemRead), .MemtoReg2(MemtoReg2), .ALUSrc(ALUSrc),
    .MemWrite(MemWrite), .EXTOp(EXTOp), .ALUop(mcu1_1_aluop), .RegWrite(RegWrite), .MemtoReg1(MemtoReg1),
    .Branch(Branch));
  ALUctrl1 aluctrl1_1 (.funcode(FUNCCODE), .ALUop(mcu1_1_aluop), .ALUctrl(ALUctrl));
endmodule
