// Logisim project D.circ as structural Verilog: 1 circuit, main circuit main
module main (
  input  CLK,
  input  D,
  output Q,
  output Q_f
);

  wire and_1_out, and_2_out, not_1_out;

  not not_1 (not_1_out, D);
  and and_1 (and_1_out, CLK, not_1_out);
  and and_2 (and_2_out, CLK, D);
  S_R_Flip_Flop s_r_ff_1 (.Q(Q), .reset(and_1_out), .Qn(Q_f), .preset(and_2_out));  // open: S, R, clk
endmodule
