// Logisim project DM.circ as structural Verilog: 1 circuit, main circuit DATAMEMORY
module DATAMEMORY (
  input  [4:0] ADDR,
  input  WE,
  input  RE,
  input  CLK,
  input  [31:0] WD,
  output [31:0] RD
);

  RAM #(.addrWidth(5), .dataWidth(32)) ram_1 (.addr(ADDR), .we(WE), .oe(RE), .clk(CLK), .din(WD), .dout(RD));
endmodule
