// Logisim project DM_lite.circ as structural Verilog: 1 circuit, main circuit DataMemory
module DataMemory (
  input  [9:0] ADDR,
  input  RE,
  input  WE,
  input  CLK,
  input  [31:0] WD,
  input  RESET,
  input  B,
  input  H,
  input  U,
  input  W,
  output [31:0] RD
);

  wire EN0, EN1, EN2, EN3, RE0, RE1, RE2, RE3, WE0, WE1, WE2, WE3;
  wire [3:0] decoder_1_out0;
  wire [3:1] decoder_2_out0;
  wire [7:0] multiplexer_5_out, RD0, RD1, RD2, RD3, WD0, WD1, WD2, WD3;
  wire [15:0] multiplexer_6_out;
  wire [31:0] bit_extender_1_out, bit_extender_2_out, bit_extender_3_out, bit_extender_4_out,
       multiplexer_1_out, multiplexer_2_out, multiplexer_7_out, multiplexer_8_out;

  Decoder #(.select(2)) decoder_1 (
    .out0(decoder_1_out0[0]), .out1(decoder_1_out0[1]), .out2(decoder_1_out0[2]), .out3(decoder_1_out0[3]),
    .sel(ADDR[1:0]), .en(B));
  Decoder decoder_2 (.out0(decoder_2_out0[1]), .out1(decoder_2_out0[3]), .sel(ADDR[1]), .en(H));
  and and_1 (WE0, WE, EN0);
  and and_2 (WE1, WE, EN1);
  and and_3 (WE2, WE, EN2);
  and and_4 (WE3, WE, EN3);
  Multiplexer #(.select(2), .width(32)) multiplexer_1 (
    .in0({{24{1'b0}}, WD[7:0]}), .in1({{16{1'b0}}, WD[7:0], {8{1'b0}}}),
    .in2({{8{1'b0}}, WD[7:0], {16{1'b0}}}), .in3({WD[7:0], {24{1'b0}}}), .out(multiplexer_1_out),
    .sel(ADDR[1:0]));
  Multiplexer #(.width(32)) multiplexer_2 (
    .in0({{16{1'b0}}, WD[15:0]}), .in1({WD[15:0], {16{1'b0}}}), .out(multiplexer_2_out), .sel(ADDR[1]));
  Multiplexer #(.select(3), .width(4)) multiplexer_3 (
    .in1(decoder_1_out0), .in2({{2{decoder_2_out0[3]}}, {2{decoder_2_out0[1]}}}), .in4({4{W}}),
    .out({EN3, EN2, EN1, EN0}), .sel({W, H, B}));  // open: in0, in3, in5, in6, in7
  RAM #(.clearpin("true"), .trigger("falling")) ram_1 (
    .addr(ADDR[9:2]), .we(WE0), .oe(RE0), .clk(CLK), .din(WD0), .dout(RD0), .clr(RESET));
  RAM #(.clearpin("true"), .trigger("falling")) ram_2 (
    .addr(ADDR[9:2]), .we(WE1), .oe(RE1), .clk(CLK), .din(WD1), .dout(RD1), .clr(RESET));
  Multiplexer #(.select(3), .width(32)) multiplexer_4 (
    .in1(multiplexer_1_out), .in2(multiplexer_2_out), .in4(WD), .out({WD3, WD2, WD1, WD0}), .sel({W, H, B}));  // open: in0, in3, in5, in6, in7
  RAM #(.clearpin("true"), .trigger("falling")) ram_3 (
    .addr(ADDR[9:2]), .we(WE2), .oe(RE2), .clk(CLK), .din(WD2), .dout(RD2), .clr(RESET));
  RAM #(.clearpin("true"), .trigger("falling")) ram_4 (
    .addr(ADDR[9:2]), .we(WE3), .oe(RE3), .clk(CLK), .din(WD3), .dout(RD3), .clr(RESET));
  and and_5 (RE0, RE, EN0);
  and and_6 (RE1, RE, EN1);
  Multiplexer #(.select(2), .width(8)) multiplexer_5 (
    .in0(RD0), .in1(RD1), .in2(RD2), .in3(RD3), .out(multiplexer_5_out), .sel(ADDR[1:0]));
  Multiplexer #(.width(16)) multiplexer_6 (.in0({RD1, RD0}), .in1({RD3, RD2}), .out(multiplexer_6_out), .sel(ADDR[1]));
  and and_7 (RE2, RE, EN2);
  and and_8 (RE3, RE, EN3);
  assign bit_extender_1_out = {{24{multiplexer_5_out[7]}}, multiplexer_5_out};  // Bit_Extender bit_extender_1
  assign bit_extender_2_out = {{24{1'b0}}, multiplexer_5_out};  // Bit_Extender bit_extender_2
  assign bit_extender_3_out = {{16{multiplexer_6_out[15]}}, multiplexer_6_out};  // Bit_Extender bit_extender_3
  assign bit_extender_4_out = {{16{1'b0}}, multiplexer_6_out};  // Bit_Extender bit_extender_4
  Multiplexer #(.width(32)) multiplexer_7 (
    .in0(bit_extender_1_out), .in1(bit_extender_2_out), .out(multiplexer_7_out), .sel(U));
  Multiplexer #(.width(32)) multiplexer_8 (
    .in0(bit_extender_3_out), .in1(bit_extender_4_out), .out(multiplexer_8_out), .sel(U));
  Multiplexer #(.select(3), .width(32)) multiplexer_9 (
    .in1(multiplexer_7_out), .in2(multiplexer_8_out), .in4({RD3, RD2, RD1, RD0}), .out(RD), .sel({W, H, B}));  // open: in0, in3, in5, in6, in7

  // Other names for the same wires on the sheet: ADDR_01[1:0] = ADDR[1:0]; ADDR_1 = ADDR[1]; ADDR_8[7:0] = ADDR[9:2]
endmodule
