// Logisim project EXMEM.circ as structural Verilog: 1 circuit, main circuit EX_MEM
module EX_MEM (
  input  CLK,
  input  RESET,
  input  overflow,
  input  JRN,
  input  lo,
  input  hi,
  input  RegDst,
  input  MemRead,
  input  MemtoReg2,
  input  JUMP,
  input  B,
  input  MemWrite,
  input  RegWrite,
  input  MemtoReg1,
  input  Branch,
  input  save31,
  input  H,
  input  W,
  input  U,
  input  Bne,
  input  [31:0] RS,
  input  [31:0] NPC4,
  input  ZF,
  input  [31:0] Result1,
  input  [31:0] Result2,
  input  [31:0] RT,
  input  [31:0] NPC3,
  input  [31:0] NPC2_1,
  input  [31:0] IR3,
  output overflow1,
  output JRN_1,
  output lo_1,
  output hi_1,
  output RegDst_1,
  output MemRead1,
  output MemtoReg2_1,
  output JUMP_1,
  output B_1,
  output MemWrite_1,
  output RegWrite_1,
  output MemtoReg1_1,
  output Branch_1,
  output save31_1,
  output H_1,
  output W_1,
  output U_1,
  output Bne1,
  output [31:0] RS1,
  output [31:0] NPC4_1,
  output ZF_1,
  output [31:0] Result1_1,
  output [31:0] Result2_1,
  output [31:0] RT_1,
  output [31:0] NPC3_1,
  output [31:0] NPC2_1_1,
  output [31:0] IR3_1
);

  Register #(.width(1)) register_1 (.D(overflow), .en(1'b1), .clk(CLK), .Q(overflow1), .clr(RESET));
  Register #(.width(1)) register_2 (.D(JRN), .en(1'b1), .clk(CLK), .Q(JRN_1), .clr(RESET));
  Register #(.width(1)) register_3 (.D(lo), .en(1'b1), .clk(CLK), .Q(lo_1), .clr(RESET));
  Register #(.width(1)) register_4 (.D(hi), .en(1'b1), .clk(CLK), .Q(hi_1), .clr(RESET));
  Register #(.width(1)) register_5 (.D(RegDst), .en(1'b1), .clk(CLK), .Q(RegDst_1), .clr(RESET));
  Register #(.width(1)) register_6 (.D(MemRead), .en(1'b1), .clk(CLK), .Q(MemRead1), .clr(RESET));
  Register #(.width(1)) register_7 (.D(MemtoReg2), .en(1'b1), .clk(CLK), .Q(MemtoReg2_1), .clr(RESET));
  Register #(.width(1)) register_8 (.D(JUMP), .en(1'b1), .clk(CLK), .Q(JUMP_1), .clr(RESET));
  Register #(.width(1)) register_9 (.D(B), .en(1'b1), .clk(CLK), .Q(B_1), .clr(RESET));
  Register #(.width(1)) register_10 (.D(MemWrite), .en(1'b1), .clk(CLK), .Q(MemWrite_1), .clr(RESET));
  Register #(.width(1)) register_11 (.D(RegWrite), .en(1'b1), .clk(CLK), .Q(RegWrite_1), .clr(RESET));
  Register #(.width(1)) register_12 (.D(MemtoReg1), .en(1'b1), .clk(CLK), .Q(MemtoReg1_1), .clr(RESET));
  Register #(.width(1)) register_13 (.D(Branch), .en(1'b1), .clk(CLK), .Q(Branch_1), .clr(RESET));
  Register #(.width(1)) register_14 (.D(save31), .en(1'b1), .clk(CLK), .Q(save31_1), .clr(RESET));
  Register #(.width(1)) register_15 (.D(H), .en(1'b1), .clk(CLK), .Q(H_1), .clr(RESET));
  Register #(.width(1)) register_16 (.D(W), .en(1'b1), .clk(CLK), .Q(W_1), .clr(RESET));
  Register #(.width(1)) register_17 (.D(U), .en(1'b1), .clk(CLK), .Q(U_1), .clr(RESET));
  Register #(.width(1)) register_18 (.D(Bne), .en(1'b1), .clk(CLK), .Q(Bne1));  // open: clr
  Register #(.width(32)) register_19 (.D(RS), .en(1'b1), .clk(CLK), .Q(RS1), .clr(RESET));
  Register #(.width(32)) register_20 (.D(NPC4), .en(1'b1), .clk(CLK), .Q(NPC4_1), .clr(RESET));
  Register #(.width(1)) register_21 (.D(ZF), .en(1'b1), .clk(CLK), .Q(ZF_1), .clr(RESET));
  Register #(.width(32)) register_22 (.D(Result1), .en(1'b1), .clk(CLK), .Q(Result1_1), .clr(RESET));
  Register #(.width(32)) register_23 (.D(Result2), .en(1'b1), .clk(CLK), .Q(Result2_1), .clr(RESET));
  Register #(.width(32)) register_24 (.D(RT), .en(1'b1), .clk(CLK), .Q(RT_1), .clr(RESET));
  Register #(.width(32)) register_25 (.D(NPC3), .en(1'b1), .clk(CLK), .Q(NPC3_1), .clr(RESET));
  Register #(.width(32)) register_26 (.D(NPC2_1), .en(1'b1), .clk(CLK), .Q(NPC2_1_1), .clr(RESET));
  Register #(.width(32)) register_27 (.D(IR3), .en(1'b1), .clk(CLK), .Q(IR3_1), .clr(RESET));
endmodule
