// Logisim project IDEX.circ as structural Verilog: 1 circuit, main circuit ID_EX
module ID_EX (
  input  CLK,
  input  JRN,
  input  RESET,
  input  judge,
  input  lo,
  input  hi,
  input  RegDst,
  input  MemRead,
  input  MemtoReg2,
  input  JUMP,
  input  B,
  input  ALUSrc,
  input  MemWrite,
  input  RegWrite,
  input  MemtoReg1,
  input  Branch,
  input  save31,
  input  H,
  input  W,
  input  V,
  input  Bne,
  input  U,
  input  [3:0] ALUctrl,
  input  [31:0] Imm32,
  input  [31:0] RT,
  input  [31:0] RS,
  input  [31:0] NPC2,
  input  [31:0] IR,
  output JRN1,
  output judge1,
  output lo1,
  output hi1,
  output RegDst1,
  output MemRead1,
  output MemtoReg21,
  output JUMP1,
  output B1,
  output ALUSrc1,
  output MemWrite1,
  output RegWrite1,
  output MemtoReg11,
  output Branch1,
  output save311,
  output H1,
  output W1,
  output V1,
  output Bne1,
  output U1,
  output [3:0] ALUctrl1,
  output [31:0] Imm321,
  output [31:0] RT1,
  output [31:0] RS1,
  output [31:0] NPC21,
  output [31:0] IR1
);

  Register #(.width(1)) register_1 (.D(JRN), .en(1'b1), .clk(CLK), .Q(JRN1), .clr(RESET));
  Register #(.width(1)) register_2 (.D(judge), .en(1'b1), .clk(CLK), .Q(judge1), .clr(RESET));
  Register #(.width(1)) register_3 (.D(lo), .en(1'b1), .clk(CLK), .Q(lo1), .clr(RESET));
  Register #(.width(1)) register_4 (.D(hi), .en(1'b1), .clk(CLK), .Q(hi1), .clr(RESET));
  Register #(.width(1)) register_5 (.D(RegDst), .en(1'b1), .clk(CLK), .Q(RegDst1), .clr(RESET));
  Register #(.width(1)) register_6 (.D(MemRead), .en(1'b1), .clk(CLK), .Q(MemRead1), .clr(RESET));
  Register #(.width(1)) register_7 (.D(MemtoReg2), .en(1'b1), .clk(CLK), .Q(MemtoReg21), .clr(RESET));
  Register #(.width(1)) register_8 (.D(JUMP), .en(1'b1), .clk(CLK), .Q(JUMP1), .clr(RESET));
  Register #(.width(1)) register_9 (.D(B), .en(1'b1), .clk(CLK), .Q(B1), .clr(RESET));
  Register #(.width(1)) register_10 (.D(ALUSrc), .en(1'b1), .clk(CLK), .Q(ALUSrc1), .clr(RESET));
  Register #(.width(1)) register_11 (.D(MemWrite), .en(1'b1), .clk(CLK), .Q(MemWrite1), .clr(RESET));
  Register #(.width(1)) register_12 (.D(RegWrite), .en(1'b1), .clk(CLK), .Q(RegWrite1), .clr(RESET));
  Register #(.width(1)) register_13 (.D(MemtoReg1), .en(1'b1), .clk(CLK), .Q(MemtoReg11), .clr(RESET));
  Register #(.width(1)) register_14 (.D(Branch), .en(1'b1), .clk(CLK), .Q(Branch1), .clr(RESET));
  Register #(.width(1)) register_15 (.D(save31), .en(1'b1), .clk(CLK), .Q(save311), .clr(RESET));
  Register #(.width(1)) register_16 (.D(H), .en(1'b1), .clk(CLK), .Q(H1), .clr(RESET));
  Register #(.width(1)) register_17 (.D(W), .en(1'b1), .clk(CLK), .Q(W1), .clr(RESET));
  Register #(.width(1)) register_18 (.D(V), .en(1'b1), .clk(CLK), .Q(V1), .clr(RESET));
  Register #(.width(1)) register_19 (.D(Bne), .en(1'b1), .clk(CLK), .Q(Bne1), .clr(RESET));
  Register #(.width(1)) register_20 (.D(U), .en(1'b1), .clk(CLK), .Q(U1), .clr(RESET));
  Register #(.width(4)) register_21 (.D(ALUctrl), .en(1'b1), .clk(CLK), .Q(ALUctrl1));  // open: clr
  Register #(.width(32)) register_22 (.D(Imm32), .en(1'b1), .clk(CLK), .Q(Imm321), .clr(RESET));
  Register #(.width(32)) register_23 (.D(RT), .en(1'b1), .clk(CLK), .Q(RT1), .clr(RESET));
  Register #(.width(32)) register_24 (.D(RS), .en(1'b1), .clk(CLK), .Q(RS1), .clr(RESET));
  Register #(.width(32)) register_25 (.D(NPC2), .en(1'b1), .clk(CLK), .Q(NPC21), .clr(RESET));
  Register #(.width(32)) register_26 (.D(IR), .en(1'b1), .clk(CLK), .Q(IR1), .clr(RESET));
endmodule
