// Logisim project IFID.circ as structural Verilog: 1 circuit, main circuit IF_ID
module IF_ID (
  input  [31:0] IR,
  input  [31:0] NPC,
  input  CLK,
  input  RESET,
  output [31:0] IR1,
  output [31:0] NPC1
);

  Register #(.width(32)) register_1 (.D(IR), .en(1'b1), .clk(CLK), .Q(IR1), .clr(RESET));
  Register #(.width(32)) register_2 (.D(NPC), .en(1'b1), .clk(CLK), .Q(NPC1), .clr(RESET));
endmodule
