// Logisim project IM.circ as structural Verilog: 1 circuit, main circuit instr_memory
module instr_memory (
  input  [4:0] addr,
  output [31:0] instr
);

  ROM #(.addrWidth(5), .dataWidth(32)) rom_1 (.addr(addr), .data(instr));
endmodule
