// Logisim project IMlite.circ as structural Verilog: 1 circuit, main circuit IM_lite
module IM_lite (
  input  [5:0] addr,
  output [31:0] instr
);

  ROM #(.addrWidth(6), .dataWidth(32)) rom_1 (.addr(addr), .data(instr));
endmodule
