// Logisim project Lite.circ as structural Verilog: 1 circuit, main circuit main
module main (
  input  reset,
  output [31:0] instr
);

  wire alu_32_1_zf, ALUSrc, and_1_out, Branch, CLK, EXTOp, MemRead, MemtoReg1, MemtoReg2, MemWrite, RegDst,
       RegWrite;
  wire [2:0] aluctrl1_1_aluctrl, mcu1_1_aluop;
  wire [4:0] MemAddr, multiplexer_1_out, pc_1_imaddr_2;
  wire [31:0] adder_1_out, adder_2_out, alu_32_1_f, bit_extender_1_out, bit_extender_2_out, datamemory_1_rd,
       MemData, multiplexer_2_out, multiplexer_3_out, multiplexer_4_out, multiplexer_5_out, pc_1_imaddr,
       RegData, register_group_32_1_rd1, shifter_1_out;

  Clock clock_1 (.out(CLK));
  instr_memory instr_memory_1 (.addr(pc_1_imaddr_2), .instr(instr));
  MCU1 mcu1_1 (
    .OP_CODE(instr[31:26]), .RegDst(RegDst), .MemRead(MemRead), .MemtoReg2(MemtoReg2), .ALUSrc(ALUSrc),
    .MemWrite(MemWrite), .EXTOp(EXTOp), .ALUop(mcu1_1_aluop), .RegWrite(RegWrite), .MemtoReg1(MemtoReg1),
    .Branch(Branch));
  ALUctrl1 aluctrl1_1 (.funcode(instr[5:0]), .ALUop(mcu1_1_aluop), .ALUctrl(aluctrl1_1_aluctrl));
  Multiplexer #(.width(5)) multiplexer_1 (
    .in0(instr[20:16]), .in1(instr[15:11]), .out(multiplexer_1_out), .sel(RegDst));
  assign bit_extender_1_out = {{16{instr[15]}}, instr[15:0]};  // Bit_Extender bit_extender_1
  assign bit_extender_2_out = {{16{1'b0}}, instr[15:0]};  // Bit_Extender bit_extender_2
  Multiplexer #(.width(32)) multiplexer_2 (
    .in0(bit_extender_1_out), .in1(bit_extender_2_out), .out(multiplexer_2_out), .sel(EXTOp));
  PC pc_1 (
    .addr(multiplexer_4_out), .clk(CLK), .RESET(reset),
    .IMaddr({pc_1_imaddr[31:7], pc_1_imaddr_2, pc_1_imaddr[1:0]}));
  register_group_32 register_group_32_1 (
    .RA1(instr[25:21]), .RA2(instr[20:16]), .WA(multiplexer_1_out), .WD(RegData), .RESET(reset), .CLK(CLK),
    .WE(RegWrite), .RD1(register_group_32_1_rd1), .RD2(MemData));
  Adder #(.width(32)) adder_1 (
    .a(32'h4), .b({pc_1_imaddr[31:7], pc_1_imaddr_2, pc_1_imaddr[1:0]}), .out(adder_1_out));  // open: cin, cout
  Shifter #(.width(32)) shifter_1 (.in(multiplexer_2_out), .\dist (5'b00010), .out(shifter_1_out));
  Multiplexer #(.width(32)) multiplexer_3 (
    .in0(MemData), .in1(multiplexer_2_out), .out(multiplexer_3_out), .sel(ALUSrc));
  Adder #(.width(32)) adder_2 (.a(adder_1_out), .b(shifter_1_out), .out(adder_2_out));  // open: cin, cout
  Multiplexer #(.width(32)) multiplexer_4 (
    .in0(adder_1_out), .in1(adder_2_out), .out(multiplexer_4_out), .sel(and_1_out));
  and and_1 (and_1_out, alu_32_1_zf, Branch);
  ALU_32 alu_32_1 (
    .A(register_group_32_1_rd1), .B(multiplexer_3_out), .OP(aluctrl1_1_aluctrl),
    .F({alu_32_1_f[31:7], MemAddr, alu_32_1_f[1:0]}), .ZF(alu_32_1_zf));  // open: SF, OF_1, CF, PF
  DATAMEMORY datamemory_1 (.ADDR(MemAddr), .WE(MemWrite), .RE(MemRead), .CLK(CLK), .WD(MemData), .RD(datamemory_1_rd));
  Multiplexer #(.width(32)) multiplexer_5 (
    .in0({alu_32_1_f[31:7], MemAddr, alu_32_1_f[1:0]}), .in1(datamemory_1_rd), .out(multiplexer_5_out),
    .sel(MemtoReg1));
  Multiplexer #(.width(32)) multiplexer_6 (
    .in0(multiplexer_5_out), .in1({instr[15:0], {16{1'b0}}}), .out(RegData), .sel(MemtoReg2));

  // Notes on the sheet:
  //   imm16
endmodule
