// Logisim project MCU.circ as structural Verilog: 1 circuit, main circuit MCU1
module MCU1 (
  input  [5:0] OP_CODE,
  output RegDst,
  output MemRead,
  output MemtoReg2,
  output ALUSrc,
  output MemWrite,
  output EXTOp,
  output [2:0] ALUop,
  output RegWrite,
  output MemtoReg1,
  output Branch
);

  wire nop, not_1_out, not_2_out, not_3_out, not_4_out, not_5_out, not_6_out, not_7_out, not_8_out,
       not_9_out, not_10_out, not_11_out, not_12_out, not_13_out, not_14_out, not_15_out, not_16_out,
       not_17_out, not_18_out, not_19_out, not_20_out, not_21_out;

  not not_1 (not_1_out, OP_CODE[0]);
  not not_2 (not_2_out, OP_CODE[1]);
  not not_3 (not_3_out, OP_CODE[3]);
  not not_4 (not_4_out, OP_CODE[4]);
  not not_5 (not_5_out, OP_CODE[5]);
  or or_1 (ALUSrc, MemRead, MemWrite, ALUop[2]);
  or or_2 (RegWrite, RegDst, MemRead, MemtoReg2, ALUop[2]);
  and and_1 (Branch, not_1_out, not_2_out, OP_CODE[2], not_3_out, not_4_out, not_5_out);
  not not_6 (not_6_out, OP_CODE[0]);
  not not_7 (not_7_out, OP_CODE[1]);
  not not_8 (not_8_out, OP_CODE[2]);
  not not_9 (not_9_out, OP_CODE[3]);
  not not_10 (not_10_out, OP_CODE[4]);
  not not_11 (not_11_out, OP_CODE[5]);
  not not_12 (not_12_out, OP_CODE[4]);
  not not_13 (not_13_out, OP_CODE[5]);
  and and_2 (RegDst, not_6_out, not_7_out, not_8_out, not_9_out, not_10_out, not_11_out);
  and and_3 (MemtoReg2, OP_CODE[0], OP_CODE[1], OP_CODE[2], OP_CODE[3], not_12_out, not_13_out);
  not not_14 (not_14_out, OP_CODE[2]);
  not not_15 (not_15_out, OP_CODE[3]);
  not not_16 (not_16_out, OP_CODE[4]);
  not not_17 (not_17_out, OP_CODE[1]);
  not not_18 (not_18_out, OP_CODE[4]);
  not not_19 (not_19_out, OP_CODE[5]);
  and and_4 (MemRead, OP_CODE[0], OP_CODE[1], not_14_out, not_15_out, not_16_out, OP_CODE[5]);
  and and_5 (ALUop[2], OP_CODE[0], not_17_out, OP_CODE[2], OP_CODE[3], not_18_out, not_19_out);
  or or_3 (ALUop[1], Branch, ALUop[2], MemtoReg2);
  or or_4 (ALUop[0], MemWrite, MemRead, ALUop[2], MemtoReg2);
  not not_20 (not_20_out, OP_CODE[2]);
  not not_21 (not_21_out, OP_CODE[4]);
  // AND_Gate nop has open pins: out=nop
  and and_6 (MemWrite, OP_CODE[0], OP_CODE[1], not_20_out, OP_CODE[3], not_21_out, OP_CODE[5]);

  assign EXTOp = ALUop[2];
  assign MemtoReg1 = MemRead;

  // Other names for the same wires on the sheet: ori = ALUop[2]; beq = Branch; lui = MemtoReg2; lw = MemRead;
  //   OP0 = OP_CODE[0]; OP1 = OP_CODE[1]; OP2 = OP_CODE[2]; OP3 = OP_CODE[3]; OP4 = OP_CODE[4]; OP5 = OP_CODE[5];
  //   R = RegDst; sw = MemWrite

  // Notes on the sheet:
  //   输入
  //   beq
  //   R
  //   lui
  //   指令译码器
  //   输出
  //   lw
  //   ori
  //   sw
  //   nop
endmodule
