// Logisim project MCU__lite.circ as structural Verilog: 1 circuit, main circuit MCU_lite
module MCU_lite (
  input  [5:0] OP_CODE,
  output RegDst,
  output MemRead,
  output MemtoReg2,
  output JUMP,
  output B,
  output [4:0] ALUop,
  output ALUSrc,
  output MemWrite,
  output EXTOp,
  output RegWrite,
  output MemtoReg1,
  output Branch,
  output save31,
  output H,
  output W,
  output U,
  output Bne
);

  wire addi, addiu, andi, beq, j, lb, lbu, lh, lhu, lw, nop, not_1_out, not_2_out, not_3_out, not_4_out,
       not_5_out, not_6_out, not_7_out, not_8_out, not_9_out, not_10_out, not_11_out, not_12_out, not_13_out,
       not_14_out, not_15_out, not_16_out, not_17_out, not_18_out, not_19_out, not_20_out, not_21_out,
       not_22_out, not_23_out, not_24_out, not_25_out, not_26_out, not_27_out, not_28_out, not_29_out,
       not_30_out, not_31_out, not_32_out, not_33_out, not_34_out, not_35_out, not_36_out, not_37_out,
       not_38_out, not_39_out, not_40_out, not_41_out, not_42_out, not_43_out, not_44_out, not_45_out,
       not_46_out, not_47_out, not_48_out, not_49_out, not_50_out, not_51_out, not_52_out, not_53_out,
       not_54_out, not_55_out, not_56_out, not_57_out, not_58_out, not_59_out, not_60_out, not_61_out,
       not_62_out, not_63_out, not_64_out, not_65_out, not_66_out, not_67_out, not_68_out, not_69_out,
       not_70_out, not_71_out, not_72_out, not_73_out, not_74_out, not_75_out, not_76_out, not_77_out,
       not_78_out, not_79_out, not_80_out, not_81_out, not_82_out, not_83_out, not_84_out, not_85_out,
       not_86_out, ori, sb, sh, slti, sltiu, sw, xori;

  not not_1 (not_1_out, OP_CODE[0]);
  not not_2 (not_2_out, OP_CODE[2]);
  not not_3 (not_3_out, OP_CODE[3]);
  not not_4 (not_4_out, OP_CODE[4]);
  not not_5 (not_5_out, OP_CODE[5]);
  not not_6 (not_6_out, OP_CODE[1]);
  not not_7 (not_7_out, OP_CODE[2]);
  not not_8 (not_8_out, OP_CODE[3]);
  not not_9 (not_9_out, OP_CODE[4]);
  not not_10 (not_10_out, OP_CODE[1]);
  not not_11 (not_11_out, OP_CODE[2]);
  not not_12 (not_12_out, OP_CODE[4]);
  not not_13 (not_13_out, OP_CODE[0]);
  not not_14 (not_14_out, OP_CODE[1]);
  not not_15 (not_15_out, OP_CODE[3]);
  not not_16 (not_16_out, OP_CODE[4]);
  not not_17 (not_17_out, OP_CODE[5]);
  not not_18 (not_18_out, OP_CODE[0]);
  not not_19 (not_19_out, OP_CODE[1]);
  not not_20 (not_20_out, OP_CODE[2]);
  not not_21 (not_21_out, OP_CODE[4]);
  not not_22 (not_22_out, OP_CODE[5]);
  or or_1 (ALUSrc, addi, addiu, andi, lb, lbu, lh, lhu, lw, ori, sb, sh, slti, sltiu, sw, xori);
  or or_2 (MemRead, lw, lb, lbu, lh, lhu);
  or or_3 (ALUop[0], j, addi, andi, Bne, lbu, ori, sh, sltiu, xori, lhu);
  or or_4 (ALUop[1], save31, addiu, andi, lb, lbu, lw, ori, slti, sltiu, j);
  and and_1 (beq, not_13_out, not_14_out, OP_CODE[2], not_15_out, not_16_out, not_17_out);
  and and_2 (addi, not_18_out, not_19_out, not_20_out, OP_CODE[3], not_21_out, not_22_out);
  and and_3 (j, not_1_out, OP_CODE[1], not_2_out, not_3_out, not_4_out, not_5_out);
  and and_4 (lh, OP_CODE[0], not_6_out, not_7_out, not_8_out, not_9_out, OP_CODE[5]);
  and and_5 (sh, OP_CODE[0], not_10_out, not_11_out, OP_CODE[3], not_12_out, OP_CODE[5]);
  or or_5 (ALUop[2], beq, Bne, lb, lbu, MemtoReg2, sb, sh, slti, sltiu);
  not not_23 (not_23_out, OP_CODE[0]);
  not not_24 (not_24_out, OP_CODE[1]);
  not not_25 (not_25_out, OP_CODE[2]);
  not not_26 (not_26_out, OP_CODE[3]);
  not not_27 (not_27_out, OP_CODE[4]);
  not not_28 (not_28_out, OP_CODE[5]);
  not not_29 (not_29_out, OP_CODE[4]);
  not not_30 (not_30_out, OP_CODE[5]);
  not not_31 (not_31_out, OP_CODE[1]);
  not not_32 (not_32_out, OP_CODE[2]);
  not not_33 (not_33_out, OP_CODE[4]);
  not not_34 (not_34_out, OP_CODE[5]);
  not not_35 (not_35_out, OP_CODE[2]);
  not not_36 (not_36_out, OP_CODE[3]);
  not not_37 (not_37_out, OP_CODE[4]);
  not not_38 (not_38_out, OP_CODE[5]);
  not not_39 (not_39_out, OP_CODE[1]);
  not not_40 (not_40_out, OP_CODE[3]);
  not not_41 (not_41_out, OP_CODE[4]);
  not not_42 (not_42_out, OP_CODE[0]);
  not not_43 (not_43_out, OP_CODE[2]);
  not not_44 (not_44_out, OP_CODE[4]);
  not not_45 (not_45_out, OP_CODE[5]);
  or or_6 (MemWrite, sw, sb, sh);
  or or_7 (MemtoReg1, lw, lb, lbu, lh, lhu);
  and and_6 (RegDst, not_23_out, not_24_out, not_25_out, not_26_out, not_27_out, not_28_out);
  and and_7 (MemtoReg2, OP_CODE[0], OP_CODE[1], OP_CODE[2], OP_CODE[3], not_29_out, not_30_out);
  and and_8 (addiu, OP_CODE[0], not_31_out, not_32_out, OP_CODE[3], not_33_out, not_34_out);
  and and_9 (save31, OP_CODE[0], OP_CODE[1], not_35_out, not_36_out, not_37_out, not_38_out);
  and and_10 (lhu, OP_CODE[0], not_39_out, OP_CODE[2], not_40_out, not_41_out, OP_CODE[5]);
  and and_11 (slti, not_42_out, OP_CODE[1], not_43_out, OP_CODE[3], not_44_out, not_45_out);
  or or_8 (EXTOp, ori, andi, xori);
  or or_9 (Branch, beq, Bne);
  or or_10 (ALUop[3], lh, lhu, lw, ori, sb, sh, slti, sltiu);
  not not_46 (not_46_out, OP_CODE[2]);
  not not_47 (not_47_out, OP_CODE[3]);
  not not_48 (not_48_out, OP_CODE[4]);
  not not_49 (not_49_out, OP_CODE[1]);
  not not_50 (not_50_out, OP_CODE[4]);
  not not_51 (not_51_out, OP_CODE[5]);
  not not_52 (not_52_out, OP_CODE[0]);
  not not_53 (not_53_out, OP_CODE[1]);
  not not_54 (not_54_out, OP_CODE[4]);
  not not_55 (not_55_out, OP_CODE[5]);
  not not_56 (not_56_out, OP_CODE[0]);
  not not_57 (not_57_out, OP_CODE[1]);
  not not_58 (not_58_out, OP_CODE[2]);
  not not_59 (not_59_out, OP_CODE[3]);
  not not_60 (not_60_out, OP_CODE[4]);
  not not_61 (not_61_out, OP_CODE[2]);
  not not_62 (not_62_out, OP_CODE[4]);
  not not_63 (not_63_out, OP_CODE[5]);
  or or_11 (ALUop[4], sw, xori, MemtoReg2, j, save31);
  and and_12 (lw, OP_CODE[0], OP_CODE[1], not_46_out, not_47_out, not_48_out, OP_CODE[5]);
  and and_13 (ori, OP_CODE[0], not_49_out, OP_CODE[2], OP_CODE[3], not_50_out, not_51_out);
  and and_14 (andi, not_52_out, not_53_out, OP_CODE[2], OP_CODE[3], not_54_out, not_55_out);
  and and_15 (lb, not_56_out, not_57_out, not_58_out, not_59_out, not_60_out, OP_CODE[5]);
  and and_16 (sltiu, OP_CODE[0], OP_CODE[1], not_61_out, OP_CODE[3], not_62_out, not_63_out);
  or or_12 (JUMP, j, save31);
  or or_13 (RegWrite, RegDst, addi, addiu, andi, save31, lb, lbu, lh, lhu, lw, ori, slti, sltiu, xori, MemtoReg2);
  not not_64 (not_64_out, OP_CODE[2]);
  not not_65 (not_65_out, OP_CODE[4]);
  not not_66 (not_66_out, OP_CODE[0]);
  not not_67 (not_67_out, OP_CODE[1]);
  not not_68 (not_68_out, OP_CODE[2]);
  not not_69 (not_69_out, OP_CODE[3]);
  not not_70 (not_70_out, OP_CODE[4]);
  not not_71 (not_71_out, OP_CODE[5]);
  not not_72 (not_72_out, OP_CODE[1]);
  not not_73 (not_73_out, OP_CODE[3]);
  not not_74 (not_74_out, OP_CODE[4]);
  not not_75 (not_75_out, OP_CODE[5]);
  not not_76 (not_76_out, OP_CODE[0]);
  not not_77 (not_77_out, OP_CODE[1]);
  not not_78 (not_78_out, OP_CODE[3]);
  not not_79 (not_79_out, OP_CODE[4]);
  not not_80 (not_80_out, OP_CODE[0]);
  not not_81 (not_81_out, OP_CODE[1]);
  not not_82 (not_82_out, OP_CODE[2]);
  not not_83 (not_83_out, OP_CODE[4]);
  not not_84 (not_84_out, OP_CODE[0]);
  not not_85 (not_85_out, OP_CODE[4]);
  not not_86 (not_86_out, OP_CODE[5]);
  and and_17 (sw, OP_CODE[0], OP_CODE[1], not_64_out, OP_CODE[3], not_65_out, OP_CODE[5]);
  and u_nop (nop, not_66_out, not_67_out, not_68_out, not_69_out, not_70_out, not_71_out);
  and and_18 (Bne, OP_CODE[0], not_72_out, OP_CODE[2], not_73_out, not_74_out, not_75_out);
  and and_19 (lbu, not_76_out, not_77_out, OP_CODE[2], not_78_out, not_79_out, OP_CODE[5]);
  and and_20 (sb, not_80_out, not_81_out, not_82_out, OP_CODE[3], not_83_out, OP_CODE[5]);
  and and_21 (xori, not_84_out, OP_CODE[1], OP_CODE[2], OP_CODE[3], not_85_out, not_86_out);
  or or_14 (B, lb, lbu, sb);
  or or_15 (H, lh, lhu, sh);
  or or_16 (W, lw, sw);
  or or_17 (U, lbu, lhu);

  // Other names for the same wires on the sheet: jal = save31; lui = MemtoReg2; OP0 = OP_CODE[0]; OP1 = OP_CODE[1];
  //   OP2 = OP_CODE[2]; OP3 = OP_CODE[3]; OP4 = OP_CODE[4]; OP5 = OP_CODE[5]; R = RegDst

  // Notes on the sheet:
  //   输入
  //   beq
  //   addi
  //   j
  //   lh
  //   sh
  //   R
  //   lui
  //   addiu
  //   jal
  //   lhu
  //   slti
  //   指令译码器
  //   输出
  //   lb
  //   sltiu
  //   lw
  //   ori
  //   andi
  //   bne
  //   lbu
  //   sb
  //   xori
  //   sw
  //   nop
endmodule
