// Logisim project MEMWB.circ as structural Verilog: 1 circuit, main circuit MEM_WB
module MEM_WB (
  input  CLK,
  input  RESET,
  input  RegDst,
  input  MemtoReg2,
  input  RegWrite,
  input  MemtoReg1,
  input  save31,
  input  of1,
  input  hi,
  input  [31:0] MemOut,
  input  [31:0] ALUout,
  input  [31:0] IR,
  input  [31:0] PC,
  output RegDst1,
  output MemtoReg2_1,
  output RegWrite_1,
  output MemtoReg1_1,
  output save31_1,
  output of1_1,
  output hi_1,
  output [31:0] MemOut1,
  output [31:0] ALUout1,
  output [31:0] IR1,
  output [31:0] PC1
);

  Register #(.width(1)) register_1 (.D(RegDst), .en(1'b1), .clk(CLK), .Q(RegDst1), .clr(RESET));
  Register #(.width(1)) register_2 (.D(MemtoReg2), .en(1'b1), .clk(CLK), .Q(MemtoReg2_1), .clr(RESET));
  Register #(.width(1)) register_3 (.D(RegWrite), .en(1'b1), .clk(CLK), .Q(RegWrite_1), .clr(RESET));
  Register #(.width(1)) register_4 (.D(MemtoReg1), .en(1'b1), .clk(CLK), .Q(MemtoReg1_1), .clr(RESET));
  Register #(.width(1)) register_5 (.D(save31), .en(1'b1), .clk(CLK), .Q(save31_1), .clr(RESET));
  Register #(.width(1)) register_6 (.D(of1), .en(1'b1), .clk(CLK), .Q(of1_1), .clr(RESET));
  Register #(.width(1)) register_7 (.D(hi), .en(1'b1), .clk(CLK), .Q(hi_1), .clr(RESET));
  Register #(.width(32)) register_8 (.D(MemOut), .en(1'b1), .clk(CLK), .Q(MemOut1), .clr(RESET));
  Register #(.width(32)) register_9 (.D(ALUout), .en(1'b1), .clk(CLK), .Q(ALUout1), .clr(RESET));
  Register #(.width(32)) register_10 (.D(IR), .en(1'b1), .clk(CLK), .Q(IR1), .clr(RESET));
  Register #(.width(32)) register_11 (.D(PC), .en(1'b1), .clk(CLK), .Q(PC1), .clr(RESET));
endmodule
