// Logisim project PCregister.circ as structural Verilog: 1 circuit, main circuit PC
module PC (
  input  [31:0] addr,
  input  clk,
  input  RESET,
  output [31:0] IMaddr
);

  Register #(.width(32)) register_1 (.D(addr), .en(1'b1), .clk(clk), .Q(IMaddr), .clr(RESET));
endmodule
