// Logisim project RAM1.circ as structural Verilog: 1 circuit, main circuit RAM_32
module RAM_32 (
  input  [7:0] ADDR,
  input  C,
  input  EN,
  input  W,
  input  [31:0] I,
  input  R,
  output [31:0] O
);

  wire R_t, W_t;

  and and_1 (W_t, W, EN);
  and and_2 (R_t, R, EN);
  RAM ram_1 (.addr(ADDR), .we(W_t), .oe(R_t), .clk(C), .din(I[7:0]), .dout(O[7:0]));
  RAM ram_2 (.addr(ADDR), .we(W_t), .oe(R_t), .clk(C), .din(I[23:16]), .dout(O[23:16]));
  RAM ram_3 (.addr(ADDR), .we(W_t), .oe(R_t), .clk(C), .din(I[15:8]), .dout(O[15:8]));
  RAM ram_4 (.addr(ADDR), .we(W_t), .oe(R_t), .clk(C), .din(I[31:24]), .dout(O[31:24]));

  // Other names for the same wires on the sheet: DATA1[7:0] = I[7:0]; DATA2[7:0] = I[15:8]; DATA3[7:0] = I[23:16];
  //   DATA4[7:0] = I[31:24]; OUTPUT1[7:0] = O[7:0]; OUTPUT2[7:0] = O[15:8]; OUTPUT3[7:0] = O[23:16];
  //   OUTPUT4[7:0] = O[31:24]

  // Notes on the sheet:
  //   输入
  //   输出
endmodule
