// Logisim project RAM_group_10.circ as structural Verilog: 1 circuit, main circuit RAM_group_10
module RAM_group_10 (
  input  [11:0] ADDR_12,
  input  [31:0] DATA,
  input  W,
  input  R,
  output [31:0] O
);

  wire C, EN1, EN2, EN3, EN4, EN5, EN6, EN7, EN8, EN9, EN10;
  wire [31:0] O1, O2, O3, O4, O5, O6, O7, O8, O9, O10;

  Clock clock_1 (.out(C));
  Decoder #(.select(4)) decoder_1 (
    .out0(EN1), .out1(EN2), .out2(EN3), .out3(EN4), .out4(EN5), .out5(EN6), .out6(EN7), .out7(EN8),
    .out8(EN9), .out9(EN10), .sel(ADDR_12[11:8]), .en(1'b1));  // open: out10, out11, out12, out13, out14, out15
  Multiplexer #(.select(4), .width(32)) multiplexer_1 (
    .in0(O1), .in1(O2), .in2(O3), .in3(O4), .in4(O5), .in5(O6), .in6(O7), .in7(O8), .in8(O9), .in9(O10),
    .out(O), .sel(ADDR_12[11:8]));  // open: in10, in11, in12, in13, in14, in15
  RAM_32 ram_32_1 (.ADDR(ADDR_12[7:0]), .C(C), .EN(EN1), .W(W), .I(DATA), .R(R), .O(O1));
  RAM_32 ram_32_2 (.ADDR(ADDR_12[7:0]), .C(C), .EN(EN2), .W(W), .I(DATA), .R(R), .O(O2));
  RAM_32 ram_32_3 (.ADDR(ADDR_12[7:0]), .C(C), .EN(EN3), .W(W), .I(DATA), .R(R), .O(O3));
  RAM_32 ram_32_4 (.ADDR(ADDR_12[7:0]), .C(C), .EN(EN4), .W(W), .I(DATA), .R(R), .O(O4));
  RAM_32 ram_32_5 (.ADDR(ADDR_12[7:0]), .C(C), .EN(EN5), .W(W), .I(DATA), .R(R), .O(O5));
  RAM_32 ram_32_6 (.ADDR(ADDR_12[7:0]), .C(C), .EN(EN6), .W(W), .I(DATA), .R(R), .O(O6));
  RAM_32 ram_32_7 (.ADDR(ADDR_12[7:0]), .C(C), .EN(EN7), .W(W), .I(DATA), .R(R), .O(O7));
  RAM_32 ram_32_8 (.ADDR(ADDR_12[7:0]), .C(C), .EN(EN8), .W(W), .I(DATA), .R(R), .O(O8));
  RAM_32 ram_32_9 (.ADDR(ADDR_12[7:0]), .C(C), .EN(EN9), .W(W), .I(DATA), .R(R), .O(O9));
  RAM_32 ram_32_10 (.ADDR(ADDR_12[7:0]), .C(C), .EN(EN10), .W(W), .I(DATA), .R(R), .O(O10));

  // Other names for the same wires on the sheet: ADDR[7:0] = ADDR_12[7:0]; ADDR_HIGH_4[3:0] = ADDR_12[11:8]
endmodule
