// Logisim project SR.circ as structural Verilog: 1 circuit, main circuit main
module main (
  input  R,
  input  S,
  output Q,
  output Q_f
);

  nor nor_1 (Q, R, Q_f);
  nor nor_2 (Q_f, Q, S);
endmodule
