// Logisim project chufaqi.circ as structural Verilog: 1 circuit, main circuit main
module main (
  input  EN,
  input  RESET,
  input  D,
  output Q
);

  wire and_1_out, clock_1_out, multiplexer_1_out;

  Clock clock_1 (.out(clock_1_out));
  Multiplexer multiplexer_1 (.in0(Q), .in1(D), .out(multiplexer_1_out), .sel(EN));
  D_Flip_Flop d_ff_1 (.D(and_1_out), .clk(clock_1_out), .Q(Q));  // open: Qn, preset, reset
  and and_1 (and_1_out, ~RESET, multiplexer_1_out);  // AND_Gate
endmodule
