// Logisim project code.circ as structural Verilog: 1 circuit, main circuit main
module main (
  input  [7:0] D_7_0,
  output [2:0] Y_2_0
);

  wire or_1_out, or_2_out, or_3_out, or_4_out, or_5_out, or_6_out;

  or or_1 (or_1_out, D_7_0[1], D_7_0[3]);
  or or_2 (or_2_out, D_7_0[2], D_7_0[3]);
  or or_3 (or_3_out, D_7_0[4], D_7_0[5]);
  or or_4 (or_4_out, or_1_out, D_7_0[5]);
  or or_5 (or_5_out, or_2_out, D_7_0[6]);
  or or_6 (or_6_out, or_3_out, D_7_0[6]);
  or or_7 (Y_2_0[0], or_4_out, D_7_0[7]);
  or or_8 (Y_2_0[1], or_5_out, D_7_0[7]);
  or or_9 (Y_2_0[2], or_6_out, D_7_0[7]);
endmodule
