// Logisim project cpu_lite.circ as structural Verilog: 1 circuit, main circuit cpu
module cpu (
  input  in_1
);

  wire alu_lite_1_of_1, alu_lite_1_zf, alucontrol_lite_1_hi, alucontrol_lite_1_jrn, alucontrol_lite_1_judge,
       alucontrol_lite_1_lo, alucontrol_lite_1_v, ALUSrc, and_1_out, B, Bne, Branch, CLK,
       ex_mem_1_memtoreg1_1, ex_mem_1_memtoreg2_1, ex_mem_1_overflow1, ex_mem_1_regdst_1,
       ex_mem_1_regwrite_1, ex_mem_1_save31_1, ex_mem_1_zf_1, EXTOp, H, hi, id_ex_1_b1, id_ex_1_bne1,
       id_ex_1_branch1, id_ex_1_h1, id_ex_1_hi1, id_ex_1_jrn1, id_ex_1_jump1, id_ex_1_lo1, id_ex_1_memread1,
       id_ex_1_memtoreg11, id_ex_1_memtoreg21, id_ex_1_memwrite1, id_ex_1_regdst1, id_ex_1_regwrite1,
       id_ex_1_save311, id_ex_1_u1, id_ex_1_w1, JRN, judge, JUMP, lo, mcu_lite_1_alusrc, mcu_lite_1_b,
       mcu_lite_1_bne, mcu_lite_1_branch, mcu_lite_1_h, mcu_lite_1_jump, mcu_lite_1_memread,
       mcu_lite_1_memtoreg1, mcu_lite_1_memtoreg2, mcu_lite_1_memwrite, mcu_lite_1_regdst,
       mcu_lite_1_regwrite, mcu_lite_1_save31, mcu_lite_1_u, mcu_lite_1_w, mem_wb_1_hi_1, mem_wb_1_of1_1,
       mem_wb_1_regwrite_1, MemRead, MemtoReg1, MemtoReg2, MemWrite, multiplexer_5_out, not_1_out, not_2_out,
       not_3_out, not_4_out, PCSrc, RegDst, RegWrite, save31, U, V, W;
  wire [2:2] and_2_out;
  wire [3:0] alucontrol_lite_1_aluctrl, id_ex_1_aluctrl1;
  wire [4:0] id_ex_1_ir1_2, mcu_lite_1_aluop, multiplexer_9_out, multiplexer_10_out;
  wire [5:0] if_id_1_ir1, if_id_1_ir1_3;
  wire [9:0] ex_mem_1_result1_1;
  wire [19:0] if_id_1_ir1_2;
  wire [21:0] ex_mem_1_result1_1_2;
  wire [26:0] id_ex_1_ir1;
  wire [31:0] add_32_2_s, alu_lite_1_f, alu_lite_1_f_2, bit_extender_1_out, bit_extender_2_out,
       bit_extender_3_out, datamemory_1_rd, ex_mem_1_ir3_1, ex_mem_1_npc2_1_1, ex_mem_1_npc3_1,
       ex_mem_1_npc4_1, ex_mem_1_result2_1, ex_mem_1_rs1, ex_mem_1_rt_1, id_ex_1_imm321, id_ex_1_npc21,
       id_ex_1_rs1, id_ex_1_rt1, if_id_1_npc1, im_lite_1_instr, mem_wb_1_aluout1, mem_wb_1_ir1,
       mem_wb_1_memout1, mem_wb_1_pc1, multiplexer_1_out, multiplexer_2_out, multiplexer_3_out,
       multiplexer_4_out, multiplexer_7_out, multiplexer_8_out, multiplexer_11_out, pc_1_imaddr, PCJUMP,
       PCnext, register_group_32_1_rd1, register_group_32_1_rd2, shifter_1_out, shifter_2_out,
       subtractor_1_out;

  Multiplexer #(.width(32)) multiplexer_1 (.in0(PCnext), .in1(PCJUMP), .out(multiplexer_1_out), .sel(PCSrc));
  PC pc_1 (.addr(multiplexer_1_out), .clk(CLK), .RESET(in_1), .IMaddr(pc_1_imaddr));
  add_32 add_32_1 (.A(pc_1_imaddr), .B(32'h4), .S(PCnext));  // open: C0, C31
  IM_lite im_lite_1 (.addr(pc_1_imaddr[7:2]), .instr(im_lite_1_instr));
  Clock clock_1 (.out(CLK));
  IF_ID if_id_1 (
    .CLK(CLK), .RESET(in_1), .IR(im_lite_1_instr), .NPC(PCnext),
    .IR1({if_id_1_ir1_3, if_id_1_ir1_2, if_id_1_ir1}), .NPC1(if_id_1_npc1));
  assign bit_extender_1_out = {{16{if_id_1_ir1_2[9]}}, {if_id_1_ir1_2[9:0], if_id_1_ir1}};  // Bit_Extender bit_extender_1
  assign bit_extender_2_out = {{16{1'b0}}, {if_id_1_ir1_2[9:0], if_id_1_ir1}};  // Bit_Extender bit_extender_2
  ALUcontrol_lite alucontrol_lite_1 (
    .funcode(if_id_1_ir1), .ALUop(mcu_lite_1_aluop), .V(alucontrol_lite_1_v), .JRN(alucontrol_lite_1_jrn),
    .ALUctrl(alucontrol_lite_1_aluctrl), .judge(alucontrol_lite_1_judge), .lo(alucontrol_lite_1_lo),
    .hi(alucontrol_lite_1_hi));
  MCU_lite mcu_lite_1 (
    .OP_CODE(if_id_1_ir1_3), .RegDst(mcu_lite_1_regdst), .MemRead(mcu_lite_1_memread),
    .MemtoReg2(mcu_lite_1_memtoreg2), .JUMP(mcu_lite_1_jump), .B(mcu_lite_1_b), .ALUop(mcu_lite_1_aluop),
    .ALUSrc(mcu_lite_1_alusrc), .MemWrite(mcu_lite_1_memwrite), .EXTOp(EXTOp),
    .RegWrite(mcu_lite_1_regwrite), .MemtoReg1(mcu_lite_1_memtoreg1), .Branch(mcu_lite_1_branch),
    .save31(mcu_lite_1_save31), .H(mcu_lite_1_h), .W(mcu_lite_1_w), .U(mcu_lite_1_u), .Bne(mcu_lite_1_bne));
  register_group_32 register_group_32_1 (
    .RESET(in_1), .CLK(CLK), .WE(RegWrite), .RA1(if_id_1_ir1_2[19:15]), .RA2(if_id_1_ir1_2[14:10]),
    .WA(multiplexer_10_out), .WD(multiplexer_11_out), .RD1(register_group_32_1_rd1),
    .RD2(register_group_32_1_rd2));
  Multiplexer #(.width(32)) multiplexer_2 (
    .in0(bit_extender_1_out), .in1(bit_extender_2_out), .out(multiplexer_2_out), .sel(EXTOp));
  ID_EX id_ex_1 (
    .RESET(in_1), .ALUSrc(mcu_lite_1_alusrc), .MemWrite(mcu_lite_1_memwrite), .RegWrite(mcu_lite_1_regwrite),
    .MemtoReg1(mcu_lite_1_memtoreg1), .Branch(mcu_lite_1_branch), .save31(mcu_lite_1_save31),
    .H(mcu_lite_1_h), .W(mcu_lite_1_w), .judge(alucontrol_lite_1_judge), .V(alucontrol_lite_1_v),
    .Bne(mcu_lite_1_bne), .U(mcu_lite_1_u), .ALUctrl(alucontrol_lite_1_aluctrl), .lo(alucontrol_lite_1_lo),
    .hi(alucontrol_lite_1_hi), .RegDst(mcu_lite_1_regdst), .MemRead(mcu_lite_1_memread),
    .MemtoReg2(mcu_lite_1_memtoreg2), .JRN(alucontrol_lite_1_jrn), .JUMP(mcu_lite_1_jump), .B(mcu_lite_1_b),
    .Imm32(multiplexer_2_out), .RT(register_group_32_1_rd1), .RS(register_group_32_1_rd2),
    .NPC2(if_id_1_npc1), .IR({if_id_1_ir1_3, if_id_1_ir1_2, if_id_1_ir1}), .CLK(CLK), .ALUSrc1(ALUSrc),
    .MemWrite1(id_ex_1_memwrite1), .RegWrite1(id_ex_1_regwrite1), .MemtoReg11(id_ex_1_memtoreg11),
    .Branch1(id_ex_1_branch1), .save311(id_ex_1_save311), .H1(id_ex_1_h1), .W1(id_ex_1_w1), .judge1(judge),
    .V1(V), .Bne1(id_ex_1_bne1), .U1(id_ex_1_u1), .ALUctrl1(id_ex_1_aluctrl1), .lo1(id_ex_1_lo1),
    .hi1(id_ex_1_hi1), .RegDst1(id_ex_1_regdst1), .MemRead1(id_ex_1_memread1),
    .MemtoReg21(id_ex_1_memtoreg21), .JRN1(id_ex_1_jrn1), .JUMP1(id_ex_1_jump1), .B1(id_ex_1_b1),
    .Imm321(id_ex_1_imm321), .RT1(id_ex_1_rt1), .RS1(id_ex_1_rs1), .NPC21(id_ex_1_npc21),
    .IR1({id_ex_1_ir1[26:6], id_ex_1_ir1_2, id_ex_1_ir1[5:0]}));
  Multiplexer #(.width(32)) multiplexer_3 (
    .in0(id_ex_1_rs1), .in1(id_ex_1_imm321), .out(multiplexer_3_out), .sel(ALUSrc));
  Subtractor #(.width(32)) subtractor_1 (.a(id_ex_1_npc21), .b(32'h4), .out(subtractor_1_out));  // open: bin, bout
  Shifter #(.width(32)) shifter_1 (.in(id_ex_1_imm321), .\dist (5'b00010), .out(shifter_1_out));
  Multiplexer #(.width(32)) multiplexer_4 (
    .in0(id_ex_1_rt1), .in1(bit_extender_3_out), .out(multiplexer_4_out), .sel(V));
  assign bit_extender_3_out = {{27{1'b0}}, id_ex_1_ir1_2};  // Bit_Extender bit_extender_3
  Shifter #(.width(32)) shifter_2 (
    .in({id_ex_1_ir1[26:6], id_ex_1_ir1_2, id_ex_1_ir1[5:0]}), .\dist (5'b00010), .out(shifter_2_out));
  add_32 add_32_2 (.A(shifter_1_out), .B(id_ex_1_npc21), .S(add_32_2_s));  // open: C0, C31
  ALU_Lite alu_lite_1 (
    .A(multiplexer_4_out), .B(multiplexer_3_out), .OP(id_ex_1_aluctrl1), .F(alu_lite_1_f),
    .ZF(alu_lite_1_zf), .OF_1(alu_lite_1_of_1), .F_2(alu_lite_1_f_2));  // open: SF, CF, PF, UOF_1
  and and_1 (and_1_out, judge, alu_lite_1_of_1);
  EX_MEM ex_mem_1 (
    .RT(id_ex_1_rs1), .NPC3({subtractor_1_out[31:28], shifter_2_out[27:0]}), .NPC2_1(id_ex_1_npc21),
    .IR3({id_ex_1_ir1[26:6], id_ex_1_ir1_2, id_ex_1_ir1[5:0]}), .overflow(and_1_out), .JRN(id_ex_1_jrn1),
    .lo(id_ex_1_lo1), .hi(id_ex_1_hi1), .RegDst(id_ex_1_regdst1), .MemRead(id_ex_1_memread1),
    .MemtoReg2(id_ex_1_memtoreg21), .JUMP(id_ex_1_jump1), .B(id_ex_1_b1), .MemWrite(id_ex_1_memwrite1),
    .RegWrite(id_ex_1_regwrite1), .MemtoReg1(id_ex_1_memtoreg11), .Branch(id_ex_1_branch1),
    .save31(id_ex_1_save311), .H(id_ex_1_h1), .W(id_ex_1_w1), .U(id_ex_1_u1), .Bne(id_ex_1_bne1), .CLK(CLK),
    .RESET(in_1), .ZF(alu_lite_1_zf), .RS(id_ex_1_rt1), .NPC4(add_32_2_s), .Result1(alu_lite_1_f),
    .Result2(alu_lite_1_f_2), .overflow1(ex_mem_1_overflow1), .JRN_1(JRN), .lo_1(lo), .hi_1(hi),
    .RegDst_1(ex_mem_1_regdst_1), .MemRead1(MemRead), .MemtoReg2_1(ex_mem_1_memtoreg2_1), .JUMP_1(JUMP),
    .B_1(B), .MemWrite_1(MemWrite), .RegWrite_1(ex_mem_1_regwrite_1), .MemtoReg1_1(ex_mem_1_memtoreg1_1),
    .Branch_1(Branch), .save31_1(ex_mem_1_save31_1), .H_1(H), .W_1(W), .U_1(U), .Bne1(Bne),
    .RS1(ex_mem_1_rs1), .NPC4_1(ex_mem_1_npc4_1), .Result1_1({ex_mem_1_result1_1_2, ex_mem_1_result1_1}),
    .Result2_1(ex_mem_1_result2_1), .RT_1(ex_mem_1_rt_1), .NPC3_1(ex_mem_1_npc3_1),
    .NPC2_1_1(ex_mem_1_npc2_1_1), .IR3_1(ex_mem_1_ir3_1), .ZF_1(ex_mem_1_zf_1));
  not not_1 (not_1_out, ex_mem_1_zf_1);
  Multiplexer multiplexer_5 (.in0(ex_mem_1_zf_1), .in1(not_1_out), .out(multiplexer_5_out), .sel(Bne));
  and and_2 (and_2_out[2], multiplexer_5_out, Branch);
  Multiplexer #(.select(3), .width(32)) multiplexer_6 (
    .in1(ex_mem_1_rs1), .in2(ex_mem_1_npc3_1), .in4(ex_mem_1_npc4_1), .out(PCJUMP),
    .sel({and_2_out[2], JUMP, JRN}));  // open: in0, in3, in5, in6, in7
  or or_1 (PCSrc, JUMP, JRN, and_2_out[2]);
  Register #(.width(32)) u_LO (.D(ex_mem_1_result2_1), .en(lo), .clk(CLK), .clr(in_1));  // open: Q
  Register #(.width(32)) u_HI (
    .D({ex_mem_1_result1_1_2, ex_mem_1_result1_1}), .en(hi), .clk(CLK), .clr(in_1));  // open: Q
  DataMemory datamemory_1 (
    .ADDR(ex_mem_1_result1_1), .RE(MemRead), .WE(MemWrite), .CLK(CLK), .WD(ex_mem_1_rt_1), .RESET(in_1),
    .B(B), .H(H), .U(U), .W(W), .RD(datamemory_1_rd));
  MEM_WB mem_wb_1 (
    .RegWrite(ex_mem_1_regwrite_1), .MemtoReg1(ex_mem_1_memtoreg1_1), .save31(ex_mem_1_save31_1),
    .of1(ex_mem_1_overflow1), .hi(hi), .RegDst(ex_mem_1_regdst_1), .MemtoReg2(ex_mem_1_memtoreg2_1),
    .MemOut(datamemory_1_rd), .ALUout({ex_mem_1_result1_1_2, ex_mem_1_result1_1}), .IR(ex_mem_1_ir3_1),
    .PC(ex_mem_1_npc2_1_1), .RESET(in_1), .CLK(CLK), .MemOut1(mem_wb_1_memout1), .ALUout1(mem_wb_1_aluout1),
    .IR1(mem_wb_1_ir1), .PC1(mem_wb_1_pc1), .RegWrite_1(mem_wb_1_regwrite_1), .MemtoReg1_1(MemtoReg1),
    .save31_1(save31), .of1_1(mem_wb_1_of1_1), .hi_1(mem_wb_1_hi_1), .RegDst1(RegDst), .MemtoReg2_1(MemtoReg2));
  not not_2 (not_2_out, mem_wb_1_of1_1);
  not not_3 (not_3_out, mem_wb_1_hi_1);
  Multiplexer #(.width(32)) multiplexer_7 (
    .in0(mem_wb_1_aluout1), .in1(mem_wb_1_memout1), .out(multiplexer_7_out), .sel(MemtoReg1));
  not not_4 (not_4_out, RegDst);
  Multiplexer #(.width(32)) multiplexer_8 (
    .in0(multiplexer_7_out), .in1({mem_wb_1_ir1[15:0], {16{1'b0}}}), .out(multiplexer_8_out), .sel(MemtoReg2));
  Multiplexer #(.width(5)) multiplexer_9 (
    .in0(mem_wb_1_ir1[15:11]), .in1(mem_wb_1_ir1[20:16]), .out(multiplexer_9_out), .sel(not_4_out));
  Multiplexer #(.width(5)) multiplexer_10 (
    .in0(multiplexer_9_out), .in1({5{1'b1}}), .out(multiplexer_10_out), .sel(save31));
  and and_3 (RegWrite, mem_wb_1_regwrite_1, not_3_out, not_2_out);
  Multiplexer #(.width(32)) multiplexer_11 (
    .in0(multiplexer_8_out), .in1(mem_wb_1_pc1), .out(multiplexer_11_out), .sel(save31));

  // Other names for the same wires on the sheet: RESET = in_1
endmodule
