// Logisim project fi.circ as structural Verilog: 1 circuit, main circuit main
module main (
  input  D0,
  input  D1,
  input  D4,
  input  D2,
  input  D3,
  input  D5,
  output Y
);

  wire and_1_out, and_2_out, or_1_out, xor_1_out;

  and and_1 (and_1_out, D0, D1);
  and and_2 (and_2_out, D2, D3);
  xor xor_1 (xor_1_out, and_1_out, and_2_out);
  or or_1 (or_1_out, D4, D5);
  xor xor_2 (Y, xor_1_out, or_1_out);
endmodule
