// Logisim project halfaddr.circ as structural Verilog: 1 circuit, main circuit halfaddr
module halfaddr (
  input  A,
  input  B,
  output C,
  output S
);

  and and_1 (C, A, B);
  xor xor_1 (S, A, B);
endmodule
