// Logisim project reg_2.circ as structural Verilog: 1 circuit, main circuit main
module main (
  input  RESET,
  input  S0,
  input  load,
  input  [7:0] in_4,
  output [7:0] out_5
);

  wire clock_1_out;

  Clock clock_1 (.out(clock_1_out));
  // Shift_Register shift_register_1: pin names not known; wires that end beside it: RESET, load, S0, clock_1_out, out_5[0], in_4[7], in_4[6], in_4[5], in_4[4], in_4[3], in_4[2], in_4[1], in_4[0], out_5[7], out_5[6], out_5[5], out_5[4], out_5[3], out_5[2], out_5[1], out_5[0]
endmodule
