// Logisim project register_1..circ as structural Verilog: 1 circuit, main circuit main
module main (
  input  WE,
  input  [7:0] in_2,
  input  OE,
  output [7:0] out_4
);

  wire clock_1_out;

  Clock clock_1 (.out(clock_1_out));
  Register register_1 (.D(in_2), .en(WE), .clk(clock_1_out), .Q(out_4), .clr(OE));
endmodule
