// Logisim project register_group.circ as structural Verilog: 1 circuit, main circuit main
module main (
  input  [3:0] RA1,
  input  [3:0] RA2,
  input  [3:0] WA,
  input  [31:0] WD,
  input  RESET,
  input  WE,
  output [31:0] RD1,
  output [31:0] RD2
);

  wire and_1_out, and_2_out, and_3_out, and_4_out, and_5_out, and_6_out, and_7_out, and_8_out, and_9_out,
       and_10_out, CLK, WA_0, WA_1, WA_2, WA_3, WA_4, WA_5, WA_6, WA_7, WA_8, WA_9;
  wire [31:0] Reg0, Reg1, Reg2, Reg3, Reg4, Reg5, Reg6, Reg7, Reg8, Reg9;

  Clock clock_1 (.out(CLK));
  Decoder #(.select(4)) decoder_1 (
    .out0(WA_0), .out1(WA_1), .out2(WA_2), .out3(WA_3), .out4(WA_4), .out5(WA_5), .out6(WA_6), .out7(WA_7),
    .out8(WA_8), .out9(WA_9), .sel(WA), .en(1'b1));  // open: out10, out11, out12, out13, out14, out15
  and and_1 (and_1_out, WE, WA_0);
  and and_2 (and_2_out, WE, WA_1);
  and and_3 (and_3_out, WE, WA_2);
  and and_4 (and_4_out, WE, WA_3);
  and and_5 (and_5_out, WE, WA_4);
  Register #(.width(32)) register_1 (.D(WD), .en(and_1_out), .clk(CLK), .Q(Reg0), .clr(RESET));
  Register #(.width(32)) register_2 (.D(WD), .en(and_2_out), .clk(CLK), .Q(Reg1), .clr(RESET));
  Register #(.width(32)) register_3 (.D(WD), .en(and_3_out), .clk(CLK), .Q(Reg2), .clr(RESET));
  Register #(.width(32)) register_4 (.D(WD), .en(and_4_out), .clk(CLK), .Q(Reg3), .clr(RESET));
  Register #(.width(32)) register_5 (.D(WD), .en(and_5_out), .clk(CLK), .Q(Reg4), .clr(RESET));
  Multiplexer #(.select(4), .width(32)) multiplexer_1 (
    .in0(Reg0), .in1(Reg1), .in2(Reg2), .in3(Reg3), .in4(Reg4), .in5(Reg5), .in6(Reg6), .in7(Reg7),
    .in8(Reg8), .in9(Reg9), .out(RD1), .sel(RA1));  // open: in10, in11, in12, in13, in14, in15
  and and_6 (and_6_out, WE, WA_5);
  and and_7 (and_7_out, WE, WA_6);
  and and_8 (and_8_out, WE, WA_7);
  and and_9 (and_9_out, WE, WA_8);
  and and_10 (and_10_out, WE, WA_9);
  Register #(.width(32)) register_6 (.D(WD), .en(and_6_out), .clk(CLK), .Q(Reg5), .clr(RESET));
  Register #(.width(32)) register_7 (.D(WD), .en(and_7_out), .clk(CLK), .Q(Reg6), .clr(RESET));
  Register #(.width(32)) register_8 (.D(WD), .en(and_8_out), .clk(CLK), .Q(Reg7), .clr(RESET));
  Register #(.width(32)) register_9 (.D(WD), .en(and_9_out), .clk(CLK), .Q(Reg8), .clr(RESET));
  Register #(.width(32)) register_10 (.D(WD), .en(and_10_out), .clk(CLK), .Q(Reg9), .clr(RESET));
  Multiplexer #(.select(4), .width(32)) multiplexer_2 (
    .in0(Reg0), .in1(Reg1), .in2(Reg2), .in3(Reg3), .in4(Reg4), .in5(Reg5), .in6(Reg6), .in7(Reg7),
    .in8(Reg8), .in9(Reg9), .out(RD2), .sel(RA2));  // open: in10, in11, in12, in13, in14, in15

  // Notes on the sheet:
  //   输入
  //   输出
  //   寄存器组
  //   片选
endmodule
