// Logisim project registergroup_32.circ as structural Verilog: 1 circuit, main circuit register_group_32
module register_group_32 (
  input  [4:0] RA1,
  input  [4:0] RA2,
  input  [4:0] WA,
  input  [31:0] WD,
  input  RESET,
  input  CLK,
  input  WE,
  output [31:0] RD1,
  output [31:0] RD2
);

  wire and_1_out, and_2_out, and_3_out, and_4_out, and_5_out, and_6_out, and_7_out, and_8_out, and_9_out,
       and_10_out, and_11_out, and_12_out, and_13_out, and_14_out, and_15_out, and_16_out, and_17_out,
       and_18_out, and_19_out, and_20_out, and_21_out, and_22_out, and_23_out, and_24_out, and_25_out,
       and_26_out, and_27_out, and_28_out, and_29_out, and_30_out, and_31_out, and_32_out, WA_0, WA_1, WA_2,
       WA_3, WA_4, WA_5, WA_6, WA_7, WA_8, WA_9, WA_10, WA_11, WA_12, WA_13, WA_14, WA_15, WA_16, WA_17,
       WA_18, WA_19, WA_20, WA_21, WA_22, WA_23, WA_24, WA_25, WA_26, WA_27, WA_28, WA_29, WA_30, WA_31;
  wire [31:0] Reg0, Reg1, Reg2, Reg3, Reg4, Reg5, Reg6, Reg7, Reg8, Reg9, Reg10, Reg11, Reg12, Reg13, Reg14,
       Reg15, Reg16, Reg17, Reg18, Reg19, Reg20, Reg21, Reg22, Reg23, Reg24, Reg25, Reg26, Reg27, Reg28,
       Reg29, Reg30, Reg31;

  and and_1 (and_1_out, WE, WA_0);
  and and_2 (and_2_out, WE, WA_1);
  and and_3 (and_3_out, WE, WA_2);
  and and_4 (and_4_out, WE, WA_3);
  and and_5 (and_5_out, WE, WA_4);
  and and_6 (and_6_out, WE, WA_10);
  and and_7 (and_7_out, WE, WA_11);
  and and_8 (and_8_out, WE, WA_12);
  and and_9 (and_9_out, WE, WA_13);
  and and_10 (and_10_out, WE, WA_14);
  and and_11 (and_11_out, WE, WA_20);
  and and_12 (and_12_out, WE, WA_21);
  and and_13 (and_13_out, WE, WA_22);
  and and_14 (and_14_out, WE, WA_23);
  and and_15 (and_15_out, WE, WA_24);
  and and_16 (and_16_out, WE, WA_30);
  Register #(.width(32)) R0 (.D(WD), .en(and_1_out), .clk(CLK), .Q(Reg0), .clr(RESET));
  Register #(.width(32)) R1 (.D(WD), .en(and_2_out), .clk(CLK), .Q(Reg1), .clr(RESET));
  Register #(.width(32)) R2 (.D(WD), .en(and_3_out), .clk(CLK), .Q(Reg2), .clr(RESET));
  Register #(.width(32)) R3 (.D(WD), .en(and_4_out), .clk(CLK), .Q(Reg3), .clr(RESET));
  Register #(.width(32)) R4 (.D(WD), .en(and_5_out), .clk(CLK), .Q(Reg4), .clr(RESET));
  Register #(.width(32)) R10 (.D(WD), .en(and_6_out), .clk(CLK), .Q(Reg10), .clr(RESET));
  Register #(.width(32)) R11 (.D(WD), .en(and_7_out), .clk(CLK), .Q(Reg11), .clr(RESET));
  Register #(.width(32)) R12 (.D(WD), .en(and_8_out), .clk(CLK), .Q(Reg12), .clr(RESET));
  Register #(.width(32)) R13 (.D(WD), .en(and_9_out), .clk(CLK), .Q(Reg13), .clr(RESET));
  Register #(.width(32)) R14 (.D(WD), .en(and_10_out), .clk(CLK), .Q(Reg14), .clr(RESET));
  Register #(.width(32)) R20 (.D(WD), .en(and_11_out), .clk(CLK), .Q(Reg20), .clr(RESET));
  Register #(.width(32)) R21 (.D(WD), .en(and_12_out), .clk(CLK), .Q(Reg21), .clr(RESET));
  Register #(.width(32)) R22 (.D(WD), .en(and_13_out), .clk(CLK), .Q(Reg22), .clr(RESET));
  Register #(.width(32)) R23 (.D(WD), .en(and_14_out), .clk(CLK), .Q(Reg23), .clr(RESET));
  Register #(.width(32)) R24 (.D(WD), .en(and_15_out), .clk(CLK), .Q(Reg24), .clr(RESET));
  Register #(.width(32)) R30 (.D(WD), .en(and_16_out), .clk(CLK), .Q(Reg30), .clr(RESET));
  and and_17 (and_17_out, WE, WA_5);
  and and_18 (and_18_out, WE, WA_6);
  and and_19 (and_19_out, WE, WA_7);
  and and_20 (and_20_out, WE, WA_8);
  and and_21 (and_21_out, WE, WA_9);
  and and_22 (and_22_out, WE, WA_15);
  and and_23 (and_23_out, WE, WA_16);
  and and_24 (and_24_out, WE, WA_17);
  and and_25 (and_25_out, WE, WA_18);
  and and_26 (and_26_out, WE, WA_19);
  and and_27 (and_27_out, WE, WA_25);
  and and_28 (and_28_out, WE, WA_26);
  and and_29 (and_29_out, WE, WA_27);
  and and_30 (and_30_out, WE, WA_28);
  and and_31 (and_31_out, WE, WA_29);
  and and_32 (and_32_out, WE, WA_31);
  Register #(.width(32)) R5 (.D(WD), .en(and_17_out), .clk(CLK), .Q(Reg5), .clr(RESET));
  Register #(.width(32)) R6 (.D(WD), .en(and_18_out), .clk(CLK), .Q(Reg6), .clr(RESET));
  Register #(.width(32)) R7 (.D(WD), .en(and_19_out), .clk(CLK), .Q(Reg7), .clr(RESET));
  Register #(.width(32)) R8 (.D(WD), .en(and_20_out), .clk(CLK), .Q(Reg8), .clr(RESET));
  Register #(.width(32)) R9 (.D(WD), .en(and_21_out), .clk(CLK), .Q(Reg9), .clr(RESET));
  Register #(.width(32)) R15 (.D(WD), .en(and_22_out), .clk(CLK), .Q(Reg15), .clr(RESET));
  Register #(.width(32)) R16 (.D(WD), .en(and_23_out), .clk(CLK), .Q(Reg16), .clr(RESET));
  Register #(.width(32)) R17 (.D(WD), .en(and_24_out), .clk(CLK), .Q(Reg17), .clr(RESET));
  Register #(.width(32)) R18 (.D(WD), .en(and_25_out), .clk(CLK), .Q(Reg18), .clr(RESET));
  Register #(.width(32)) R19 (.D(WD), .en(and_26_out), .clk(CLK), .Q(Reg19), .clr(RESET));
  Register #(.width(32)) R25 (.D(WD), .en(and_27_out), .clk(CLK), .Q(Reg25), .clr(RESET));
  Register #(.width(32)) R26 (.D(WD), .en(and_28_out), .clk(CLK), .Q(Reg26), .clr(RESET));
  Register #(.width(32)) R27 (.D(WD), .en(and_29_out), .clk(CLK), .Q(Reg27), .clr(RESET));
  Register #(.width(32)) R28 (.D(WD), .en(and_30_out), .clk(CLK), .Q(Reg28), .clr(RESET));
  Register #(.width(32)) R29 (.D(WD), .en(and_31_out), .clk(CLK), .Q(Reg29), .clr(RESET));
  Register #(.width(32)) R31 (.D(WD), .en(and_32_out), .clk(CLK), .Q(Reg31), .clr(RESET));
  Decoder #(.select(5)) decoder_1 (
    .out0(WA_0), .out1(WA_1), .out2(WA_2), .out3(WA_3), .out4(WA_4), .out5(WA_5), .out6(WA_6), .out7(WA_7),
    .out8(WA_8), .out9(WA_9), .out10(WA_10), .out11(WA_11), .out12(WA_12), .out13(WA_13), .out14(WA_14),
    .out15(WA_15), .out16(WA_16), .out17(WA_17), .out18(WA_18), .out19(WA_19), .out20(WA_20), .out21(WA_21),
    .out22(WA_22), .out23(WA_23), .out24(WA_24), .out25(WA_25), .out26(WA_26), .out27(WA_27), .out28(WA_28),
    .out29(WA_29), .out30(WA_30), .out31(WA_31), .sel(WA), .en(1'b1));
  Multiplexer #(.select(5), .width(32)) multiplexer_1 (
    .in0(Reg0), .in1(Reg1), .in2(Reg2), .in3(Reg3), .in4(Reg4), .in5(Reg5), .in6(Reg6), .in7(Reg7),
    .in8(Reg8), .in9(Reg9), .in10(Reg10), .in11(Reg11), .in12(Reg12), .in13(Reg13), .in14(Reg14),
    .in15(Reg15), .in16(Reg16), .in17(Reg17), .in18(Reg18), .in19(Reg19), .in20(Reg20), .in21(Reg21),
    .in22(Reg22), .in23(Reg23), .in24(Reg24), .in25(Reg25), .in26(Reg26), .in27(Reg27), .in28(Reg28),
    .in29(Reg29), .in30(Reg30), .in31(Reg31), .out(RD2), .sel(RA2));
  Multiplexer #(.select(5), .width(32)) multiplexer_2 (
    .in0(Reg0), .in1(Reg1), .in2(Reg2), .in3(Reg3), .in4(Reg4), .in5(Reg5), .in6(Reg6), .in7(Reg7),
    .in8(Reg8), .in9(Reg9), .in10(Reg10), .in11(Reg11), .in12(Reg12), .in13(Reg13), .in14(Reg14),
    .in15(Reg15), .in16(Reg16), .in17(Reg17), .in18(Reg18), .in19(Reg19), .in20(Reg20), .in21(Reg21),
    .in22(Reg22), .in23(Reg23), .in24(Reg24), .in25(Reg25), .in26(Reg26), .in27(Reg27), .in28(Reg28),
    .in29(Reg29), .in30(Reg30), .in31(Reg31), .out(RD1), .sel(RA1));

  // Notes on the sheet:
  //   输入
  //   输出
  //   寄存器组
  //   片选
endmodule
